// Digital circuit Complex Fixed Division.dig as structural Verilog
module Complex_Fixed_Division (
  input  a_re,
  input  a_im,
  input  b_re,
  input  b_im,
  output y_re,
  output y_im
);

  wire fixed_adder_1_s, fixed_adder_2_s, fixed_multiply_1_p, fixed_multiply_2_p, fixed_multiply_3_p,
       fixed_multiply_4_p, fixed_multiply_5_p, fixed_multiply_6_p, fixed_subtract_1_s;

  Fixed_Multiply #(.generic("bits := args.bits; radix := args.radix; round := true; saturate := true; signed := true;")) fixed_multiply_1 (
    .a(a_re), .b(b_re), .p(fixed_multiply_1_p));
  Fixed_Multiply #(.generic("bits := args.bits; radix := args.radix; round := true; saturate := true; signed := true;")) fixed_multiply_2 (
    .a(a_im), .b(b_im), .p(fixed_multiply_2_p));
  Fixed_Multiply #(.generic("bits := args.bits; radix := args.radix; round := true; saturate := true; signed := true;")) fixed_multiply_3 (
    .a(a_im), .b(b_re), .p(fixed_multiply_3_p));
  Fixed_Multiply #(.generic("bits := args.bits; radix := args.radix; round := true; saturate := true; signed := true;")) fixed_multiply_4 (
    .a(a_re), .b(b_im), .p(fixed_multiply_4_p));
  Fixed_Multiply #(.generic("bits := args.bits; radix := args.radix; round := true; saturate := true; signed := true;")) fixed_multiply_5 (
    .a(b_re), .b(b_re), .p(fixed_multiply_5_p));
  Fixed_Multiply #(.generic("bits := args.bits; radix := args.radix; round := true; saturate := true; signed := true;")) fixed_multiply_6 (
    .a(b_im), .b(b_im), .p(fixed_multiply_6_p));
  Fixed_Adder #(.generic("bits := args.bits; radix := args.radix; saturate := true; signed := true;")) fixed_adder_1 (
    .a(fixed_multiply_1_p), .b(fixed_multiply_2_p), .s(fixed_adder_1_s));
  Fixed_Subtract #(.generic("bits := args.bits; radix := args.radix; saturate := true; signed := true;")) fixed_subtract_1 (
    .a(fixed_multiply_3_p), .b(fixed_multiply_4_p), .s(fixed_subtract_1_s));
  Fixed_Adder #(.generic("bits := args.bits; radix := args.radix; saturate := true; signed := true;")) fixed_adder_2 (
    .a(fixed_multiply_5_p), .b(fixed_multiply_6_p), .s(fixed_adder_2_s));
  Fixed_Divide #(.generic("bits := args.bits; radix := args.radix; round := true; saturate := true; signed := true;")) fixed_divide_1 (
    .a(fixed_adder_1_s), .b(fixed_subtract_1_s), .q(y_re));
  Fixed_Divide #(.generic("bits := args.bits; radix := args.radix; round := true; saturate := true; signed := true;")) fixed_divide_2 (
    .a(fixed_subtract_1_s), .b(fixed_adder_2_s), .q(y_im));
endmodule

/* Code that sets the parameters or builds the circuit:
bits := 16;
radix := 8;
*/
