// Digital circuit Complex Fixed Magnitude.dig as structural Verilog
module Complex_Fixed_Magnitude (
  input  re_in,
  input  im_in,
  output mag
);

  wire add_1_s, dynamic_fixed_multiply_1_p, dynamic_fixed_multiply_2_p;

  Dynamic_Fixed_Multiply #(.generic("a_bits := args.bits; a_radix := args.radix; b_bits := args.bits; b_radix := args.radix; signed := true;")) dynamic_fixed_multiply_1 (
    .a(re_in), .b(re_in), .p(dynamic_fixed_multiply_1_p));
  Dynamic_Fixed_Multiply #(.generic("a_bits := args.bits; a_radix := args.radix; b_bits := args.bits; b_radix := args.radix; signed := true;")) dynamic_fixed_multiply_2 (
    .a(im_in), .b(im_in), .p(dynamic_fixed_multiply_2_p));
  Add #(.generic("this.Bits = global.mul_bits;")) add_1 (
    .a(dynamic_fixed_multiply_1_p), .b(dynamic_fixed_multiply_2_p), .c_i(1'b0), .s(add_1_s));  // open: c_o
  Dynamic_Fixed_Square_Root #(.generic("bits := global.mul_bits; radix := global.mul_radix;")) dynamic_fixed_square_root_1 (
    .in(add_1_s), .out(mag));
endmodule

/* Code that sets the parameters or builds the circuit:
bits := 16;
radix := 8;
*/

/* Code that sets the parameters or builds the circuit:
global.mul_bits := args.bits * 2;
global.mul_radix := args.radix * 2;
*/
