// Digital circuit Complex Fixed Multiply.dig as structural Verilog
module Complex_Fixed_Multiply (
  input  a_re,
  input  a_im,
  input  b_re,
  input  b_im,
  output y_re,
  output y_im
);

  wire fixed_multiply_1_p, fixed_multiply_2_p, fixed_multiply_3_p, fixed_multiply_4_p;

  Fixed_Multiply #(.generic("bits := args.bits; radix := args.radix; round := true; saturate := true; signed := true;")) fixed_multiply_1 (
    .a(a_re), .b(b_re), .p(fixed_multiply_1_p));
  Fixed_Multiply #(.generic("bits := args.bits; radix := args.radix; round := true; saturate := true; signed := true;")) fixed_multiply_2 (
    .a(a_im), .b(b_im), .p(fixed_multiply_2_p));
  Fixed_Multiply #(.generic("bits := args.bits; radix := args.radix; round := true; saturate := true; signed := true;")) fixed_multiply_3 (
    .a(a_im), .b(b_re), .p(fixed_multiply_3_p));
  Fixed_Multiply #(.generic("bits := args.bits; radix := args.radix; round := true; saturate := true; signed := true;")) fixed_multiply_4 (
    .a(a_re), .b(b_im), .p(fixed_multiply_4_p));
  Fixed_Subtract #(.generic("bits := args.bits; radix := args.radix; saturate := true; signed := true;")) fixed_subtract_1 (
    .a(fixed_multiply_1_p), .b(fixed_multiply_2_p), .s(y_re));
  Fixed_Adder #(.generic("bits := args.bits; radix := args.radix; saturate := true; signed := true;")) fixed_adder_1 (
    .a(fixed_multiply_3_p), .b(fixed_multiply_4_p), .s(y_im));
endmodule

/* Code that sets the parameters or builds the circuit:
bits := 16;
radix := 8;
*/
