// Digital circuit Complex Fixed Square.dig as structural Verilog
module Complex_Fixed_Square (
  input  re_in,
  input  im_in,
  output re_out,
  output im_out
);

  wire dynamic_fixed_scalb_1_out, fixed_multiply_1_p, fixed_multiply_2_p, fixed_multiply_3_p;

  Fixed_Multiply #(.generic("bits := args.bits; radix := args.radix; round := true; saturate := true; signed := true;")) fixed_multiply_1 (
    .a(re_in), .b(re_in), .p(fixed_multiply_1_p));
  Fixed_Multiply #(.generic("bits := args.bits; radix := args.radix; round := true; saturate := true; signed := true;")) fixed_multiply_2 (
    .a(im_in), .b(im_in), .p(fixed_multiply_2_p));
  Fixed_Multiply #(.generic("bits := args.bits; radix := args.radix; round := true; saturate := true; signed := true;")) fixed_multiply_3 (
    .a(im_in), .b(re_in), .p(fixed_multiply_3_p));
  Fixed_Subtract #(.generic("bits := args.bits; radix := args.radix; saturate := true; signed := true;")) fixed_subtract_1 (
    .a(fixed_multiply_1_p), .b(fixed_multiply_2_p), .s(re_out));
  Dynamic_Fixed_Scalb #(.generic("bits := args.bits; radix := args.radix; scale := 1; signed := true;")) dynamic_fixed_scalb_1 (
    .in(fixed_multiply_3_p), .out(dynamic_fixed_scalb_1_out));
  Fixed_Resize #(.generic("in_bits := args.bits + 1; in_radix := args.radix; out_bits := args.bits; out_radix := args.radix; round := false; saturate := true; signed := true;")) fixed_resize_1 (
    .in(dynamic_fixed_scalb_1_out), .out(im_out));
endmodule

/* Code that sets the parameters or builds the circuit:
bits := 16;
radix := 8;
*/
