// Digital circuit Complex Fixed Subtract.dig as structural Verilog
module Complex_Fixed_Subtract (
  input  a_re,
  input  a_im,
  input  b_re,
  input  b_im,
  output y_re,
  output y_im
);

  Fixed_Subtract #(.generic("bits := args.bits; radix := args.radix; saturate := true; signed := true;")) fixed_subtract_1 (
    .a(a_re), .b(b_re), .s(y_re));
  Fixed_Subtract #(.generic("bits := args.bits; radix := args.radix; saturate := true; signed := true;")) fixed_subtract_2 (
    .a(a_im), .b(b_im), .s(y_im));
endmodule

/* Code that sets the parameters or builds the circuit:
bits := 16;
radix := 8;
*/
