// Digital circuit Dynamic Fixed Absolute.dig as structural Verilog
// The Dynamic Fixed Absolute returns the positive number.
// The output has 1 bit more than the input.
// {{de 
// Der Dynamic Fixed Absolute gibt die positive Zahl zurück.
// Die Ausgabe hat 1 Bit mehr als die Eingabe.
// }}
module Dynamic_Fixed_Absolute (
  input  in,
  output out
);

  wire fixed_resize_1_out;

  Fixed_Resize #(.generic("in_bits := args.bits; in_radix := args.radix; out_bits := global.out_bits; out_radix := args.radix; round := false; saturate := false; signed := true;")) fixed_resize_1 (
    .in(in), .out(fixed_resize_1_out));
  Absolute #(.generic("bits := global.out_bits;")) absolute_1 (.in(fixed_resize_1_out), .out(out));
endmodule

/* Code that sets the parameters or builds the circuit:
bits := 16;
radix := 8;
*/

/* Code that sets the parameters or builds the circuit:
global.out_bits := args.bits + 1;
*/
