// Digital circuit Dynamic Fixed Divide.dig as structural Verilog
// The Dynamic Fixed Divide returns the quotient of a and b.
// This circuit is the equivalent of the VHDL standard library "fixed_generic_pkg".
// a, b can have different bit width and radix, where s is the bit width of "a_bits + b_bits".
// If "signed = True", the radix of s is "args.a_radix + (args.b_bits - args.b_radix) - 1".
// If "signed = False", the radix of s is "args.a_radix + (args.b_bits - args.b_radix)".
// If "round = true", the result will be rounded.
// If "b = 0" the largest possible number is output.
// {{de 
// Der Dynamic Fixed Divide gibt den Quotient von a und b zurück.
// Dieser Schaltkreis is das Äquivalent von der VHDL Standard Bibliothek "fixed_generic_pkg"
// a, b können eine unterschiedliche Bitbreite und Radix haben, wobei s die Bitbreite von "a_bits + b_bits" hat.
// Falls "signed = True", ist der Radix von s "args.a_radix + (args.b_bits - args.b_radix) - 1".
// Falls "signed = False", ist der Radix von s "args.a_radix + (args.b_bits - args.b_radix)".
// Falls "round = true" ist, wird das Ergebnis gerundet.
// Falls "b = 0" die größtmögliche Zahl ausgegeben.
// }}
module Dynamic_Fixed_Divide (
  input  a,
  input  b,
  output q
);

  wire comparator_1_eq, div_1_q, fixed_resize_1_out, fixed_resize_2_out, fixed_resize_3_out;

  Fixed_Resize #(.generic("in_bits := args.a_bits; in_radix := args.a_radix; out_bits := global.div_bits; out_radix := global.div_in_radix; round := false; saturate := false; signed := args.signed;")) fixed_resize_1 (
    .in(a), .out(fixed_resize_1_out));
  Fixed_Resize #(.generic("in_bits := args.b_bits; in_radix := args.b_radix; out_bits := global.div_bits; out_radix := args.b_radix; round := false; saturate := false; signed := args.signed;")) fixed_resize_2 (
    .in(b), .out(fixed_resize_2_out));
  Comparator #(.generic("this.Bits = args.b_bits; this.Signed = args.signed;")) comparator_1 (
    .a(b), .b(1'b0), .eq(comparator_1_eq));  // open: gt, lt
  Div #(.generic("this.Bits = global.div_bits; this.Signed = args.signed;")) div_1 (
    .a(fixed_resize_1_out), .b(fixed_resize_2_out), .q(div_1_q));  // open: r
  Fixed_Resize #(.generic("in_bits := global.div_bits; in_radix := global.div_out_radix; out_bits := global.out_bits; out_radix := global.out_radix; round := args.round; saturate := false; signed := args.signed;")) fixed_resize_3 (
    .in(div_1_q), .out(fixed_resize_3_out));
  Multiplexer #(.generic("this.Bits = global.out_bits;")) multiplexer_1 (
    .sel(comparator_1_eq), .in_0(fixed_resize_3_out), .in_1(1'b1), .out(q));
endmodule

/* Code that sets the parameters or builds the circuit:
a_bits := 16;
a_radix := 8;
b_bits := 16;
b_radix := 8;
round := true;
signed := true;
*/

/* Code that sets the parameters or builds the circuit:
global.out_bits := args.a_bits + args.b_bits;

guard_bits := 3;

if (args.signed) {
    global.out_radix := args.a_radix + (args.b_bits - args.b_radix) - 1;
    
    global.div_bits  := global.out_bits + guard_bits;
    global.div_in_radix := args.a_radix + args.b_bits + guard_bits - 1;
    global.div_out_radix := global.out_radix + guard_bits;
    
    global.saturate := !(1 << (global.out_bits - 1));

    global.fixed_format := 8;
} else {
    global.out_radix := args.a_radix + (args.b_bits - args.b_radix);

    global.div_bits := global.out_bits + guard_bits;
    global.div_in_radix := args.a_radix + args.b_bits + guard_bits;
    global.div_out_radix := global.out_radix + guard_bits;
    
    global.saturate := !(1 << global.out_bits);

    global.fixed_format := 7;
}
*/
