// Digital circuit Dynamic Fixed Multiply.dig as structural Verilog
// The Dynamic Fixed Multiply returns the product of a and b.
// This circuit is the equivalent of the VHDL standard library "fixed_generic_pkg".
// a, b can have different bit width and radix, where s has the bit width of "2 * max(a_bits, b_bits)" and radix "a_radix + b_radix".
// {{de 
// Der Dynamic Fixed Multiply gibt das Produkt von a und b zurück.
// Dieser Schaltkreis is das Äquivalent von der VHDL Standard Bibliothek "fixed_generic_pkg"
// a, b können eine unterschiedliche Bitbreite und Radix haben, wobei s die Bitbreite von "2 * max(a_bits, b_bits)" und Radix "a_radix + b_radix" hat.
// }}
module Dynamic_Fixed_Multiply (
  input  a,
  input  b,
  output p
);

  wire fixed_resize_1_out, fixed_resize_2_out, mul_1_mul;

  Fixed_Resize #(.generic("in_bits := args.a_bits; in_radix := args.a_radix; out_bits := global.mul_in_bits; out_radix := args.a_radix; round := false; saturate := false; signed := args.signed;")) fixed_resize_1 (
    .in(a), .out(fixed_resize_1_out));
  Fixed_Resize #(.generic("in_bits := args.b_bits; in_radix := args.b_radix; out_bits := global.mul_in_bits; out_radix := args.b_radix; round := false; saturate := false; signed := args.signed;")) fixed_resize_2 (
    .in(b), .out(fixed_resize_2_out));
  Mul #(.Signed("true"), .generic("this.Bits = global.mul_in_bits; this.Signed = args.signed;")) mul_1 (
    .a(fixed_resize_1_out), .b(fixed_resize_2_out), .mul(mul_1_mul));
  Fixed_Resize #(.generic("in_bits := global.mul_out_bits; in_radix := global.out_radix; out_bits := global.out_bits; out_radix := global.out_radix; round := false; saturate := false; signed := args.signed;")) fixed_resize_3 (
    .in(mul_1_mul), .out(p));
endmodule

/* Code that sets the parameters or builds the circuit:
a_bits := 16;
a_radix := 8;
b_bits := 16;
b_radix := 8;
signed := true;
*/

/* Code that sets the parameters or builds the circuit:
if (args.signed) {
    global.fixed_format := 8;
} else {
    global.fixed_format := 7;
}

global.out_bits := args.a_bits + args.b_bits;
global.out_radix := args.a_radix + args.b_radix;

global.mul_in_bits := max(args.a_bits, args.b_bits);
global.mul_out_bits := 2 * global.mul_in_bits;
*/
