// Digital circuit Dynamic Fixed Negation.dig as structural Verilog
// The Dynamic Fixed Negation returns the negative number.
// The output has 1 bit more than the input.
// {{de 
// Der Dynamic Fixed Negation gibt die negative Zahl zurück.
// Die Ausgabe hat 1 Bit mehr als die Eingabe.
// }}
module Dynamic_Fixed_Negation (
  input  in,
  output out
);

  wire fixed_resize_1_out;

  Fixed_Resize #(.generic("in_bits := args.bits; in_radix := args.radix; out_bits := global.out_bits; out_radix := args.radix; round := false; saturate := false; signed := true;")) fixed_resize_1 (
    .in(in), .out(fixed_resize_1_out));
  Neg #(.generic("this.Bits = global.out_bits;")) neg_1 (.in(fixed_resize_1_out), .out(out));
endmodule

/* Code that sets the parameters or builds the circuit:
bits := 16;
radix := 8;
*/

/* Code that sets the parameters or builds the circuit:
global.out_bits := args.bits + 1;
*/
