// Digital circuit Dynamic Fixed Scalb.dig as structural Verilog
// The Dynamic Fixed Scalb scales the result with a power of 2. 
// {{de Der Dynamic Fixed Scalb skaliert das Ergebnis mit einer Potenz von 2.}}
module Dynamic_Fixed_Scalb (
  input  in,
  output out
);

  wire fixed_resize_1_out;

  Fixed_Resize #(.generic("in_bits := args.bits; in_radix := args.radix; out_bits := global.out_bits; out_radix := global.out_radix; round := false; saturate := false; signed := args.signed;")) fixed_resize_1 (
    .in(in), .out(fixed_resize_1_out));
  BarrelShifter #(.barrelShifterMode("arithmetic"), .barrelSigned("true"), .generic("this.Bits = global.out_bits; this.barrelShifterMode = global.shift_mode;")) barrelshifter_1 (
    .in(fixed_resize_1_out), .shift(1'b1), .out(out));
endmodule

/* Code that sets the parameters or builds the circuit:
bits := 16;
radix := 8;
scale := 5;
signed := true;
*/

/* Code that sets the parameters or builds the circuit:
if (args.signed) {
    global.fixed_format := 8;
    global.shift_mode := 2;
} else {
    global.fixed_format := 7;
    global.shift_mode := 0;
}

global.out_bits := args.bits + abs(args.scale);
global.out_radix := args.radix + abs(args.scale);
*/
