// Digital circuit Dynamic Fixed Square Root.dig as structural Verilog
// The Dynamic Fixed Square Root outputs the root.
// The result bit width is "ceil(bits / 2)" and radix "ceil(radix / 2)".
// {{de 
// Der Dynamic Fixed Square Root gibt die Wurzel aus.
// Die Ergebniss Bitbreite ist "ceil(bits / 2)" und Radix "ceil(radix / 2)".
// }}
module Dynamic_Fixed_Square_Root (
  input  in,
  output out
);

  Square_Root #(.generic("bits := args.bits;")) square_root_1 (.in(in));
endmodule

/* Code that sets the parameters or builds the circuit:
bits := 16;
radix := 8;
*/

/* Code that sets the parameters or builds the circuit:
global.out_bits := ceil(args.bits / 2);
global.out_radix := ceil(args.radix / 2);
*/
