// Digital circuit Dynamic Fixed Subtract.dig as structural Verilog
// The Dynamic Fixed Subtract returns the difference between a and b.
// This circuit is the equivalent of the VHDL standard library "fixed_generic_pkg".
// a, b can have different bit width and radix, where s has bit width of "max(a_bits, b_bits) + 1" and radix has "max(a_radix, b_radix)".
// {{de 
// Der Dynamic Fixed Subtract gibt die Differenz von a und b zurück.
// Dieser Schaltkreis is das Äquivalent von der VHDL Standard Bibliothek "fixed_generic_pkg"
// a, b können eine unterschiedliche Bitbreite und Radix haben, wobei s die Bitbreite von "max(a_bits, b_bits) + 1" und Radix "max(a_radix, b_radix)" hat.
// }}
module Dynamic_Fixed_Subtract (
  input  a,
  input  b,
  output s
);

  wire fixed_resize_1_out, fixed_resize_2_out;

  Fixed_Resize #(.generic("in_bits := args.a_bits; in_radix := args.a_radix; out_bits := global.out_bits; out_radix := global.out_radix; round := false; saturate := false; signed := args.signed;")) fixed_resize_1 (
    .in(a), .out(fixed_resize_1_out));
  Fixed_Resize #(.generic("in_bits := args.b_bits; in_radix := args.b_radix; out_bits := global.out_bits; out_radix := global.out_radix; round := false; saturate := false; signed := args.signed;")) fixed_resize_2 (
    .in(b), .out(fixed_resize_2_out));
  Sub #(.generic("this.Bits = global.out_bits;")) sub_1 (
    .a(fixed_resize_1_out), .b(fixed_resize_2_out), .c_i(1'b0), .s(s));  // open: c_o
endmodule

/* Code that sets the parameters or builds the circuit:
a_bits := 16;
a_radix := 8;
b_bits := 16;
b_radix := 8;
signed := true;
*/

/* Code that sets the parameters or builds the circuit:
if (args.signed) {
    global.fixed_format := 8;
} else {
    global.fixed_format := 7;
}

global.out_bits := max(args.a_bits, args.b_bits) + 1;
global.out_radix := max(args.a_radix, args.b_radix);
*/
