// Digital circuit Dynamic Fixed Divide Test.dig as structural Verilog
module Dynamic_Fixed_Divide_Test (
  input  [15:0] sfxt16_8_in,
  input  [15:0] sfxt16_8_in_2,
  input  [15:0] ufxt16_8_in,
  input  [15:0] ufxt16_8_in_2,
  output [31:0] ufxt32_16_out,
  output [31:0] sfxt32_15_out,
  output [31:0] ufxt32_16_out_2,
  output [31:0] sfxt32_15_out_2
);

  Foo #(.applicationType("GHDL")) u_Foo (.a(sfxt16_8_in), .b(sfxt16_8_in_2), .o(sfxt32_15_out));
  Fixed_Divide #(.generic("a_bits := 16; a_radix := 8; b_bits := 16; b_radix := 8; signed := true;")) fixed_divide_1 (
    .a(sfxt16_8_in), .b(sfxt16_8_in_2), .q(sfxt32_15_out_2));
  Foo #(.applicationType("GHDL")) u_Foo_2 (.a(ufxt16_8_in), .b(ufxt16_8_in_2), .o(ufxt32_16_out_2));
  Fixed_Divide #(.generic("a_bits := 16; a_radix := 8; b_bits := 16; b_radix := 8; signed := false;")) fixed_divide_2 (
    .a(ufxt16_8_in), .b(ufxt16_8_in_2), .q(ufxt32_16_out));

  // Notes on the sheet:
  //   sfxt16_8_in: default 256
  //   sfxt16_8_in_2: default 256
  //   ufxt16_8_in: default 256
  //   ufxt16_8_in_2: default 256
endmodule

/* Code of Foo:
library IEEE;
use IEEE.STD_LOGIC_1164.ALL;
use IEEE.fixed_pkg.ALL;
use IEEE.NUMERIC_STD.all;

entity Foo is
    port(a : in STD_LOGIC_VECTOR (16-1 downto 0);
         b : in STD_LOGIC_VECTOR (16-1 downto 0);
         o : out STD_LOGIC_VECTOR (32-1 downto 0)
    );
end Foo;

architecture Bar of Foo is
    signal fa : sfixed(8-1 downto -8);
    signal fb : sfixed(8-1 downto -8);
    signal fo : sfixed(17-1 downto -15);
begin
    fa <= to_sfixed(a, fa'high, fa'low);
    fb <= to_sfixed(b, fb'high, fb'low);
    fo <= fa / fb;
    o <= to_slv(fa / fb);
end Bar;

--ufixed(7 downto -8) / ufixed(7 downto -8) = ufixed(7--8 downto -8-7-1) = 16-1 downto -16
--sfixed(a downto b) / sfixed(c downto d) = sfixed(7--8+1 downto -8-7)   = 17-1 downto -15
*/

/* Code of Foo:
library IEEE;
use IEEE.STD_LOGIC_1164.ALL;
use IEEE.fixed_pkg.ALL;
use IEEE.NUMERIC_STD.all;

entity Foo is
    port(a : in STD_LOGIC_VECTOR (16-1 downto 0);
         b : in STD_LOGIC_VECTOR (16-1 downto 0);
         o : out STD_LOGIC_VECTOR (32-1 downto 0)
    );
end Foo;

architecture Bar of Foo is
    signal fa : ufixed(8-1 downto -8);
    signal fb : ufixed(8-1 downto -8);
    signal fo : ufixed(16-1 downto -16);
begin
    fa <= to_ufixed(a, fa'high, fa'low);
    fb <= to_ufixed(b, fb'high, fb'low);
    fo <= fa / fb;
    o <= to_slv(fa / fb);
end Bar;

--ufixed(7 downto -8) / ufixed(7 downto -8) = ufixed(7--8 downto -8-7-1) = 16-1 downto -16
--sfixed(a downto b) / sfixed(c downto d) = sfixed(7--8+1 downto -8-7)   = 17-1 downto -15
*/
