// Digital circuit Fixed Adder.dig as structural Verilog
// The Fixed Adder returns the sum of a and b.
// a, b and c have the same bit width and radix.
// If "saturate = true", the largest possible number is output at overflow, if "false" the upper bits are truncated.
// {{de 
// Der Fixed Adder gibt die Summe von a und b zurück.
// a, b und c haben die gleiche Bitbreite und Radix.
// Falls "saturate = true" ist, wird beim overflow die größt mögliche Zahl ausgegeben, wenn "false" werden die oberen Bits abgeschnitten.
// }}
module Fixed_Adder (
  input  a,
  input  b,
  output s
);

  wire add_1_s, fixed_resize_1_out, fixed_resize_2_out;

  Fixed_Resize #(.generic("in_bits := args.bits; in_radix := args.radix; out_bits := global.add_bits; out_radix := args.radix; round := false; saturate := false; signed := args.signed;")) fixed_resize_1 (
    .in(a), .out(fixed_resize_1_out));
  Fixed_Resize #(.generic("in_bits := args.bits; in_radix := args.radix; out_bits := global.add_bits; out_radix := args.radix; round := false; saturate := false; signed := args.signed;")) fixed_resize_2 (
    .in(b), .out(fixed_resize_2_out));
  Add #(.generic("this.Bits = global.add_bits;")) add_1 (
    .a(fixed_resize_1_out), .b(fixed_resize_2_out), .c_i(1'b0), .s(add_1_s));  // open: c_o
  Fixed_Resize #(.generic("in_bits := global.add_bits; in_radix := args.radix; out_bits := args.bits; out_radix := args.radix; round := false; saturate := args.saturate; signed := args.signed;")) fixed_resize_3 (
    .in(add_1_s), .out(s));
endmodule

/* Code that sets the parameters or builds the circuit:
bits := 4;
radix := 2;
saturate := true;
signed := true;
*/

/* Code that sets the parameters or builds the circuit:
if (args.signed) {
    global.fixed_format := 8;
} else {
    global.fixed_format := 7;
}

global.add_bits := args.bits + 1;
*/
