// Digital circuit Fixed Divide.dig as structural Verilog
// The Fixed Divide returns the quotient of a and b.
// a, b and c have the same bit width and radix.
// If "saturate = true", the largest possible number is output at overflow, if "false" the upper bits are truncated.
// If "round = true", the result will be rounded.
// If "b = 0" the largest possible number is output.
// {{de 
// Der Fixed Divide gibt den Quotient von a und b zurück.
// a, b und c haben die gleiche Bitbreite und Radix.
// Falls "saturate = true" ist, wird beim overflow die größt mögliche Zahl ausgegeben, wenn "false" werden die oberen Bits abgeschnitten.
// Falls "round = true" ist, wird das Ergebnis gerundet.
// Falls "b = 0" die größtmögliche Zahl ausgegeben.
// }}
module Fixed_Divide (
  input  a,
  input  b,
  output q
);

  wire comparator_1_eq, div_1_q, fixed_resize_1_out, fixed_resize_2_out, fixed_resize_3_out;

  Fixed_Resize #(.generic("in_bits := args.bits; in_radix := args.radix; out_bits := global.div_bits; out_radix := global.div_in_radix; round := false; saturate := false; signed := args.signed;")) fixed_resize_1 (
    .in(a), .out(fixed_resize_1_out));
  Fixed_Resize #(.generic("in_bits := args.bits; in_radix := args.radix; out_bits := global.div_bits; out_radix := args.radix; round := false; saturate := false; signed := args.signed;")) fixed_resize_2 (
    .in(b), .out(fixed_resize_2_out));
  Comparator #(.generic("this.Bits = args.bits; this.Signed = args.signed;")) comparator_1 (
    .a(b), .b(1'b0), .eq(comparator_1_eq));  // open: gt, lt
  Div #(.generic("this.Bits = global.div_bits; this.Signed = args.signed;")) div_1 (
    .a(fixed_resize_1_out), .b(fixed_resize_2_out), .q(div_1_q));  // open: r
  Fixed_Resize #(.generic("in_bits := global.div_bits; in_radix := global.div_out_radix; out_bits := args.bits; out_radix := args.radix; round := args.round; saturate := args.saturate; signed := args.signed;")) fixed_resize_3 (
    .in(div_1_q), .out(fixed_resize_3_out));
  Multiplexer #(.generic("this.Bits = args.bits;")) multiplexer_1 (
    .sel(comparator_1_eq), .in_0(fixed_resize_3_out), .in_1(1'b1), .out(q));
endmodule

/* Code that sets the parameters or builds the circuit:
bits := 16;
radix := 8;
round := true;
saturate := true;
signed := true;
*/

/* Code that sets the parameters or builds the circuit:
if (args.signed) {
    global.saturate := !(1 << (args.bits - 1));
    global.fixed_format := 8;
} else {
    global.saturate := !(1 << args.bits);
    global.fixed_format := 7;
}

global.div_bits  := 2 * args.bits;
global.div_in_radix := args.radix + args.bits;
global.div_out_radix := args.bits;
*/
