// Digital circuit Fixed Multiply.dig as structural Verilog
// The Fixed Multiply returns the product of a and b.
// a and b have the same bit width and radix, where p has twice the bit width and radix.
// If "saturate = true", the largest possible number is output at overflow, if "false" the upper bits are truncated.
// If "round = true", the result will be rounded.
// {{de 
// Der Fixed Multiply gibt das Produkt von a und b zurück.
// a, b und c haben die gleiche Bitbreite und Radix.
// Falls "saturate = true" ist, wird beim overflow die größt mögliche Zahl ausgegeben, wenn "false" werden die oberen Bits abgeschnitten.
// Falls "round = true" ist, wird das Ergebnis gerundet.
// }}
module Fixed_Multiply (
  input  a,
  input  b,
  output p
);

  wire mul_1_mul;

  Mul #(.Signed("true"), .generic("this.Bits = global.mul_in_bits; this.Signed = args.signed;")) mul_1 (
    .a(a), .b(b), .mul(mul_1_mul));
  Fixed_Resize #(.generic("in_bits := global.mul_out_bits; in_radix := global.mul_out_radix; out_bits := args.bits; out_radix := args.radix; round := args.round; saturate := args.saturate; signed := args.signed;")) fixed_resize_1 (
    .in(mul_1_mul), .out(p));
endmodule

/* Code that sets the parameters or builds the circuit:
bits := 16;
radix := 8;
round := true;
saturate := true;
signed := true;
*/

/* Code that sets the parameters or builds the circuit:
if (args.signed) {
    global.fixed_format := 8;
} else {
    global.fixed_format := 7;
}

global.mul_in_bits := args.bits;
global.mul_out_bits := 2 * args.bits;
global.mul_out_radix := 2 * args.radix;
*/
