// Digital circuit Fixed To Integer.dig as structural Verilog
// Fixed To Integer converts the input to a number without radix.
// If "round = true", the result is rounded.
// If "saturate = true" the largest possible number is output at overflow, if "false" the upper bits are truncated.
// {{de 
// Fixed To Integer wandelt die Eingabe um zu einer Zahl ohne Radix.
// Falls "round = true" ist, wird das Ergebnis gerundet.
// Falls "saturate = true" ist, wird beim overflow die größtmögliche Zahl ausgegeben, wenn "false" werden die oberen Bits abgeschnitten.
// }}
module Fixed_To_Integer (
  input  in,
  output out
);

  Fixed_Resize #(.generic("in_bits := args.in_bits; in_radix := args.in_radix; out_bits := args.out_bits; out_radix := 0; round := args.round; saturate := false; signed := args.signed;")) fixed_resize_1 (
    .in(in), .out(out));
endmodule

/* Code that sets the parameters or builds the circuit:
in_bits := 16;
in_radix := 8;
out_bits := 8;
round := true;
saturate := true;
signed := true;
*/

/* Code that sets the parameters or builds the circuit:
if (args.signed) {
    global.int_format := 2;
    global.fixed_format := 8;
} else {
    global.int_format := 1;
    global.fixed_format := 7;
}
*/
