// Digital circuit Integer To Fixed.dig as structural Verilog
// Integer To Fixed converts the input to a number with radix.
// {{de Integer To Fixed wandelt die Eingabe um zu einer Zahl mit Radix.}}
module Integer_To_Fixed (
  input  in,
  output out
);

  Fixed_Resize #(.generic("in_bits := args.in_bits; in_radix := 0; out_bits := args.out_bits; out_radix := args.out_radix; round := false; saturate := false; signed := args.signed;")) fixed_resize_1 (
    .in(in), .out(out));
endmodule

/* Code that sets the parameters or builds the circuit:
in_bits := 8;
out_bits := 16;
out_radix := 8;
signed := true;
*/

/* Code that sets the parameters or builds the circuit:
if (args.signed) {
    global.int_format := 2;
    global.fixed_format := 8;
} else {
    global.int_format := 1;
    global.fixed_format := 7;
}
*/
