// Digital circuit Float Adder.dig as structural Verilog
module Float_Adder (
  input  [31:0] a,
  input  [31:0] b,
  output [31:0] s
);

  wire adder_subtractor_1_p4, and_1_out, and_2_out, and_3_out, and_4_out, and_5_out, and_6_out,
       comparator_1_lt, comparator_2_eq, distance_1_s, float_break_number_1_sign, float_break_number_2_sign,
       multiplexer_6_out, multiplexer_7_out, or_1_out, or_2_out, or_3_out, or_4_out, or_5_out,
       or_reduce_1_out, or_reduce_2_p1, priorityencoder_1_any, xor_1_out;
  wire [0:0] multiplexer_5_out, or_6_out;
  wire [1:0] priorityencoder_1_num;
  wire [3:0] float_break_number_1_fptype, float_break_number_2_fptype, rom_1_d, rom_2_d;
  wire [5:0] find_rightmost_1_pos;
  wire [7:0] bitextender_1_out, distance_1_d, float_break_number_1_exp, float_break_number_2_exp,
       multiplexer_3_out, sub_1_s;
  wire [23:0] float_break_number_1_mnt, float_break_number_2_mnt;
  wire [26:0] multiplexer_5_out_2;
  wire [27:0] barrelshifter_1_out, multiplexer_1_out, multiplexer_2_out;
  wire [31:0] float_normalize_1_p5, multiplexer_4_out;

  Float_Break_Number float_break_number_1 (
    .arg(a), .fptype(float_break_number_1_fptype), .sign(float_break_number_1_sign),
    .exp(float_break_number_1_exp), .mnt(float_break_number_1_mnt));
  Float_Break_Number float_break_number_2 (
    .arg(b), .fptype(float_break_number_2_fptype), .sign(float_break_number_2_sign),
    .exp(float_break_number_2_exp), .mnt(float_break_number_2_mnt));
  ROM #(.AddrBits(4), .Bits(4)) rom_1 (.A(float_break_number_1_fptype), .sel(1'b1), .D(rom_1_d));
  ROM #(.AddrBits(4), .Bits(4)) rom_2 (.A(float_break_number_2_fptype), .sel(1'b1), .D(rom_2_d));
  Distance #(.generic("bits := 8; signed := true;")) distance_1 (
    .a(float_break_number_1_exp), .b(float_break_number_2_exp), .d(distance_1_d), .s(distance_1_s));
  Comparator #(.Bits(28)) comparator_1 (
    .a({1'b0, float_break_number_1_mnt, 3'b000}), .b({1'b0, float_break_number_2_mnt, 3'b000}),
    .lt(comparator_1_lt));  // open: gt, eq
  Comparator #(.Signed("true"), .Bits(8)) comparator_2 (
    .a({8{1'b0}}), .b(distance_1_d), .eq(comparator_2_eq));  // open: gt, lt
  and and_1 (and_1_out, rom_1_d[1], rom_2_d[1]);
  or or_1 (or_1_out, rom_2_d[2], rom_1_d[2]);
  or or_2 (or_2_out, rom_1_d[0], rom_2_d[0]);
  and and_2 (and_2_out, rom_1_d[0], rom_2_d[2]);
  and and_3 (and_3_out, rom_1_d[2], rom_2_d[0]);
  or or_3 (or_3_out, rom_1_d[3], rom_2_d[3]);
  and and_4 (and_4_out, comparator_1_lt, comparator_2_eq);
  or or_4 (or_4_out, and_2_out, and_3_out, or_3_out);
  Multiplexer #(.Bits(28)) multiplexer_1 (
    .sel(or_5_out), .in_0({1'b0, float_break_number_1_mnt, 3'b000}),
    .in_1({1'b0, float_break_number_2_mnt, 3'b000}), .out(multiplexer_1_out));
  Multiplexer #(.Bits(28)) multiplexer_2 (
    .sel(or_5_out), .in_0({1'b0, float_break_number_2_mnt, 3'b000}),
    .in_1({1'b0, float_break_number_1_mnt, 3'b000}), .out(multiplexer_2_out));
  or or_5 (or_5_out, and_4_out, distance_1_s);
  Multiplexer #(.Bits(8)) multiplexer_3 (
    .sel(distance_1_s), .in_0(float_break_number_1_exp), .in_1(float_break_number_2_exp),
    .out(multiplexer_3_out));
  PriorityEncoder #(.Selector_Bits(2)) priorityencoder_1 (
    .in0(and_1_out), .in1(or_1_out), .in2(or_2_out), .in3(or_4_out), .num(priorityencoder_1_num),
    .any(priorityencoder_1_any));
  Find_Rightmost #(.generic("bits := 28;")) find_rightmost_1 (
    .arg(multiplexer_2_out), .val(1'b1), .pos(find_rightmost_1_pos));
  Multiplexer #(.Selector_Bits(2), .Bits(32)) multiplexer_4 (
    .sel(priorityencoder_1_num), .in_0(32'h80000000), .in_1(32'hff800000), .in_2(32'h7f800000),
    .in_3(32'h7f800001), .out(multiplexer_4_out));
  BarrelShifter #(.Bits(28), .direction("right")) barrelshifter_1 (
    .in(multiplexer_2_out), .shift(distance_1_d[4:0]), .out(barrelshifter_1_out));
  Or_Reduce #(.generic("bits := 2;")) or_reduce_1 (.in(distance_1_d[6:5]), .out(or_reduce_1_out));
  BitExtender #(.inputBits(6), .outputBits(8)) bitextender_1 (.in(find_rightmost_1_pos), .out(bitextender_1_out));
  Multiplexer #(.Bits(28)) multiplexer_5 (
    .sel(or_reduce_1_out), .in_0(barrelshifter_1_out), .in_1({28{1'b0}}),
    .out({multiplexer_5_out_2, multiplexer_5_out[0]}));
  Sub #(.Bits(8)) sub_1 (.a(bitextender_1_out), .b(distance_1_d), .c_i(1'b1), .s(sub_1_s));  // open: c_o
  or or_6 (or_6_out[0], multiplexer_5_out[0], and_5_out);
  and and_5 (and_5_out, ~find_rightmost_1_pos[5], sub_1_s[7]);  // And
  Multiplexer multiplexer_6 (
    .sel(or_5_out), .in_0(float_break_number_1_sign), .in_1(float_break_number_2_sign),
    .out(multiplexer_6_out));
  xor xor_1 (xor_1_out, float_break_number_2_sign, float_break_number_1_sign);
  Multiplexer multiplexer_7 (
    .sel(xor_1_out), .in_0(float_break_number_1_sign), .in_1(multiplexer_6_out), .out(multiplexer_7_out));
  // Adder_Subtractor #(.generic("bits := 28;")) adder_subtractor_1: pin names not known; wires that end beside it: multiplexer_1_out, {multiplexer_5_out_2, or_6_out[0]}, xor_1_out, adder_subtractor_1_p4
  and and_6 (and_6_out, multiplexer_7_out, or_reduce_2_p1);
  // Or_Reduce #(.generic("bits := 28;")) or_reduce_2: pin names not known; wires that end beside it: or_reduce_2_p1, adder_subtractor_1_p4
  // Float_Normalize #(.generic("exponent_bits := 8; round_style := args.round_style;")) float_normalize_1: pin names not known; wires that end beside it: adder_subtractor_1_p4, multiplexer_3_out, and_6_out, and_5_out, float_normalize_1_p5
  Multiplexer #(.Bits(32)) multiplexer_8 (
    .sel(priorityencoder_1_any), .in_0(float_normalize_1_p5), .in_1(multiplexer_4_out), .out(s));

  // Notes on the sheet:
  //   Special Cases
  //   contents of rom_1 (hex, n*v repeats v):
  //   0,1,0,0,2,4,0,0,8,8
  //   Significant Swap
  //   contents of rom_2 (hex, n*v repeats v):
  //   0,1,0,0,2,4,0,0,8,8
  //   Alignment
  //   if (a == quiet_nan | a == nan | b == quiet_nan | b == nan
  //   | (a == pos_inf & b == neg_inf) | (a == neg_inf & b == pos_inf))
  //   result = quiet_nan
  //   else if (a == pos_inf | b == pos_inf)
  //   result = pos_inf
  //   else if (a == neg_inf | b == neg_inf)
  //   result = neg_inf
  //   else if (a == neg_zero & b == neg_zero)
  //   result = neg_zero
  //   else
  //   s = a + b
  //   Sign Control
endmodule

/* Test case cancellation-and-subnorm:
a b s
0x02400000 0x82800000 0x81800000
0x82c00000 0x03000000 0x02000000
0x03400000 0x83800000 0x82800000
0x85c00000 0x06000000 0x05000000
0x87000000 0x06c00000 0x86000000
0x08400000 0x88800000 0x87800000
0x8b000000 0x0ac00000 0x8a000000
0x00400000 0x80800000 0x80400000
0x811b9db8 0x011b9db7 0x80000002
0x813ffffe 0x01800000 0x00800004
0x033fffff 0x83800000 0x82800002
0x041ba938 0x841ba937 0x00000080
0x051d1cba 0x851d1cba 0x00000000
0x053ffffe 0x85800000 0x84800004
0x86800000 0x063ffffe 0x85800004
0x86c00000 0x07000000 0x06000000
0x87400000 0x07800000 0x06800000
0x083d9efa 0x883d9efb 0x80008000
0x08a8d2d2 0x88a8d2d1 0x00010000
0x899ac7b5 0x099ac7b6 0x00040000
0x09bfffff 0x8a000000 0x89000002
0x0a800000 0x8a3ffffe 0x09800004
0x8b800000 0x0b3fffff 0x8a800002
0x8033afe8 0x0033afe7 0x80000001
0x81800001 0x013fffff 0x80800006
0x020c3f1a 0x820c3f18 0x00000010
0x03000000 0x82bffffe 0x02000004
0x03bffffe 0x84000001 0x83000008
0x08000000 0x87bffffe 0x07000004
0x093edd7c 0x893edd7e 0x80040000
0x0a2f54de 0x8a2f54de 0x00000000
0x0a8bb898 0x8a8bb897 0x00100000
0x8b3272e5 0x0b3272e4 0x80200000
0x80100000 0x00100000 0x00000000
0x802a9ed6 0x002a9ed4 0x80000002
0x8100ab04 0x0100ab01 0x80000006
0x82095d92 0x02095d96 0x00000020
0x05b080e1 0x85b080df 0x00000800
0x06385fee 0x86385ff0 0x80001000
0x072041be 0x872041c2 0x80008000
0x879fc43e 0x079fc441 0x0000c000
0x08800000 0x883ffffb 0x0780000a
0x09208142 0x8920813f 0x00060000
0x80080000 0x00080000 0x00000000
0x0095b5af 0x8095b5a9 0x00000006
0x810f81a4 0x010f819d 0x8000000e
0x8196232a 0x01962330 0x00000018
0x02000002 0x81bffff8 0x01000018
0x02800002 0x823ffffa 0x01800014
0x032da1d6 0x832da1dd 0x800000e0
0x83800002 0x033ffffa 0x82800014
0x04009001 0x84009006 0x80000280
0x84bffff6 0x05000002 0x0400001c
0x058ce498 0x858ce49f 0x80001c00
0x06805880 0x86805886 0x80006000
0x07bffff6 0x88000003 0x87000020
0x08800004 0x883fffff 0x07800012
0x890f191d 0x090f1922 0x000a0000
0x093ffffe 0x89800006 0x8880001c
0x09bffff8 0x8a000003 0x8900001c
0x0008ce42 0x8008ce42 0x00000000
0x0104a817 0x8104a808 0x0000001e
0x82167729 0x02167733 0x00000050
0x83000006 0x02bffff0 0x82000038
0x04000002 0x83bffff2 0x03000024
0x852e09df 0x052e09d4 0x80001600
0x05800000 0x853fffe4 0x04800038
0x863fffea 0x06800001 0x05800030
0x86bffffd 0x07000008 0x06000026
0x88800004 0x083fffea 0x8780003c
0x802e52e2 0x002e52d8 0x8000000a
0x8100000e 0x00bfffe2 0x8040003a
0x82359ad2 0x02359af0 0x000000f0
0x82800006 0x023fffe4 0x81800050
0x0329e646 0x8329e65b 0x800002a0
0x03800010 0x833fffec 0x02800068
0x83bffff1 0x04000009 0x03000042
0x04be05ec 0x84be05fc 0x80001000
0x053df2fc 0x853df2ea 0x00002400
0x05b65a70 0x85b65a54 0x00007000
0x0611ab1e 0x8611ab30 0x80009000
0x86800008 0x063fffec 0x85800048
0x87b46fd5 0x07b46fed 0x00060000
0x07bfffc5 0x88000000 0x87000076
0x89000012 0x08bffffb 0x88000052
0x00010000 0x80010000 0x00000000
0x8006b0ec 0x0006b0ee 0x00000002
0x80080004 0x0007fffe 0x80000006
0x000ffffa 0x80100008 0x8000000e
0x002727dc 0x802727ca 0x00000012
0x0095419b 0x809541ca 0x8000002f
0x02bfffcc 0x83000010 0x820000a8
0x04000010 0x83bfffb4 0x030000d8
0x852dafe5 0x052dafc2 0x80004600
0x853fffa4 0x05800000 0x048000b8
0x05bfffa7 0x86000003 0x850000be
0x8680002e 0x063fffea 0x858000e4
0x07299de0 0x87299dbb 0x0004a000
0x083ffffe 0x8880003c 0x878000f4
0x80020002 0x00020000 0x80000002
0x0007fffe 0x80080006 0x80000008
0x801c0686 0x001c069e 0x00000018
0x00800042 0x803ffffa 0x00400048
0x8213f202 0x0213f279 0x000003b8
0x82bfffd1 0x0300003a 0x02000146
0x038ba404 0x838ba46c 0x80001a00
0x8400003f 0x03bfffd2 0x83000158
0x843fffff 0x0480006c 0x038001b2
0x85bfffdc 0x0600004b 0x05000174
0x870b59f6 0x070b5982 0x800e8000
0x883915fc 0x0839159c 0x80300000
0x00004000 0x80004000 0x00000000
0x0000fffe 0x80010002 0x80000004
0x80078810 0x00078803 0x8000000d
0x8007fff8 0x00080009 0x00000011
0x00190698 0x801906c6 0x8000002e
0x802a72f0 0x002a7360 0x00000070
0x808000e5 0x003ffffc 0x804000e9
0x012bf1b6 0x812bf2a2 0x800001d8
0x81bdb746 0x01bdb802 0x000002f0
0x82bacf98 0x02bad089 0x00000f10
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*/

/* Test case alignment:
a b s
0x0480feb9 0x1236205f 0x1236205f
0x153bf2d9 0x221d0a49 0x221d0a49
0x2510165e 0x318737dc 0x318737dc
0x050aea7e 0x112e01c6 0x112e01c7
0x0585de9e 0x1114ebb0 0x1114ebb1
0x5580d2bd 0x60bbd59a 0x60bbd59c
0x563bc6dd 0x60a2bf84 0x60a2bf8a
0x660fea62 0x700cad16 0x700cad1f
0x758ade82 0x7f339700 0x7f339711
0x072ca33c 0x10177d41 0x10177d6c
0x1727975c 0x1fbe672a 0x1fbe677e
0x173bfae0 0x1f2854be 0x1f28557a
0x00000a3f 0x028fa8e6 0x028fa98a
0x331f7e5f 0x3a36b2d0 0x3a36b54e
0x6b9a327e 0x721d5cba 0x721d618c
0x5415269e 0x5a0446a4 0x5a044ff6
0x43a94a23 0x492e7437 0x492e8960
0x44243e43 0x49151e21 0x49154731
0x141f3262 0x18bc080a 0x18bc57a3
0x009a0682 0x04a311f4 0x04a3abfb
0x15153aa2 0x1889fbde 0x188b2653
0x14a91e27 0x17b3e972 0x17b68deb
0x658b22e2 0x68178fb2 0x681be8c9
0x7585d702 0x77beb99c 0x77c7170c
0x71aea660 0x7325edc4 0x733bc290
0x718289e4 0x728fdb58 0x72b07dd1
0x51bdbe04 0x5236c542 0x528ad222
0x5238b224 0x521daf2c 0x52ab30a8
0x12b36644 0x12049915 0x12f5b2ce
0x06ae7a64 0x05aba2ff 0x06d96324
0x06829de8 0x05159092 0x06954ffa
0x12bd5208 0x10bc7a7c 0x12c919b0
0x63384628 0x60a36466 0x633d614b
0x63b37a48 0x608a0e50 0x63b5a281
0x43ae4e68 0x4031183a 0x43afb098
0x24294287 0x20180223 0x2429da89
0x442436a7 0x3fbeec0d 0x4424961d
0x100ce606 0x0b264036 0x100d0f96
0x2087da25 0x1b0d2a20 0x2087ebca
0x501bddaa 0x4a3737b2 0x501be91d
0x2096d1ca 0x1a1e219c 0x2096d6bb
0x5111c5ea 0x4a04cb86 0x5111c7fd
0x710cba09 0x69abf570 0x710cbb61
0x7187ae29 0x6992df5a 0x7187aebc
0x611bf1ae 0x58bceced 0x611bf20c
0x4196a5ce 0x38a396d7 0x4196a5f7
0x421199ee 0x388a80c0 0x421199ff
0x420c8e0d 0x38316aaa 0x420c8e18
0x332e52c8 0x289510eb 0x332e52cd
0x1a82964c 0x0fbf5e7e 0x1a82964f
0x3eab05ab 0x3326b2a7 0x3eab05ac
0x6f2619ca 0x630d7c90 0x6f2619cb
0x3f210dea 0x32b4667a 0x3f210dea
0x2f353170 0x221e540e 0x2f353170
0x4fb0258f 0x42057df8 0x4fb0258f
0x132b39ae 0x21ac07e1 0x21ac07e1
0x61a5edce 0x419331cb 0x61a5edce
*/

/* Test case cancellation:
a b s
0xbcbffffe 0x3d000000 0x3c000004
0x2f87fb11 0xaf87fb10 0x24000000
0x3b3ffffc 0xbb800001 0xba80000c
0x4f3ffffc 0xcf800002 0xce800010
0x8b80002a 0x0b3fffe8 0x8a8000d8
0x123fff36 0x92800037 0x91800270
0xe13ffddb 0x6180035a 0x608011b2
0x04bffe1f 0x85001470 0x84005582
0x673f8562 0xe78014a9 0xe68147e0
0xcabedfcc 0x4b006286 0x4a03ca80
0xdf19614a 0x5f17de6a 0xdbc17000
0xab2d43d8 0x2b2b0317 0xa8103040
0x5e8df69c 0xde94ed9d 0xdc5ee020
0x8090e190 0x0099734b 0x000891bb
0xaa35e086 0x2a03147d 0xa94b3024
0x14400000 0x94800000 0x93800000
0xf00e7d9d 0x700e7d9c 0xe4800000
0x5b000000 0xdabffffe 0x5a000004
0x2b3ffffe 0xab800001 0xaa800008
0x6f31ef65 0xef31ef5e 0x64e00000
0xa31423af 0x231423a4 0x99300000
0x4819acbe 0xc819acac 0x3e900000
0xc6a53d9f 0x46a53de9 0x3e140000
0x9a34ec91 0x1a34ebae 0x92630000
0xc03ffbee 0x40800168 0x3f800dc4
0xf025b216 0x7025c1b4 0x6a79e000
0x3c3faabe 0xbc8005c0 0xbb80c184
0x7cbf4c29 0xfd001be3 0xfc01d73a
0x778175f8 0xf73637d8 0x76996830
0x9e1cebe4 0x1e357186 0x1cc42d10
0xf200b51e 0x6f3e7739 0xf1fb7682
0xddb0dec8 0x55888880 0xddb0de3f
0x591aed32 0x60bfffc6 0x60c000fc
*/

/* Code that sets the parameters or builds the circuit:
round_style := 0;
*/
