// Digital circuit Float Break Number.dig as structural Verilog
module Float_Break_Number (
  input  [31:0] arg,
  output [3:0] fptype,
  output sign,
  output [7:0] exp,
  output [23:0] mnt
);

  wire [0:0] rom_1_d;
  wire [7:7] not_1_out;

  Float_Classify float_classify_1 (.arg(arg), .fptype(fptype));
  ROM #(.AddrBits(4), .Bits(2)) rom_1 (.A(fptype), .sel(1'b1), .D({mnt[23], rom_1_d[0]}));
  not not_1 (not_1_out[7], arg[30]);
  Multiplexer #(.Selector_Bits(2), .Bits(8)) multiplexer_1 (
    .sel({mnt[23], rom_1_d[0]}), .in_0(8'h81), .in_1(8'h81), .in_2({not_1_out[7], arg[29:23]}),
    .in_3({8{1'b1}}), .out(exp));

  assign mnt[22:0] = arg[22:0];
  assign sign = arg[31];

  // Notes on the sheet:
  //   if (arg == pos_zero | arg == neg_zero)
  //   exp = 0x81
  //   mnt = arg_mnt
  //   else if (arg == pos_denormal | arg == neg_denormal)
  //   exp = 0x81
  //   mnt = arg_mnt
  //   else if (arg == pos_normal | arg == neg_normal
  //   | arg == pos_inf | arg == neg_inf)
  //   exp = arg_exp
  //   mnt = 1 + arg_mnt
  //   else
  //   exp = 0xff
  //   mnt = 1 + arg_mnt
  //   contents of rom_1 (hex, n*v repeats v):
  //   0,2,2,1,0,2,2,1,8*3
endmodule
