// Digital circuit Float Check Round.dig as structural Verilog
module Float_Check_Round (
  input  fract,
  input  [2:0] gurads,
  input  sticky,
  input  sign,
  output round
);

  wire and_1_out, and_2_out, and_3_out, or_1_out, or_reduce_1_out, or_reduce_2_p2;

  Or_Reduce #(.generic("bits := 2;")) or_reduce_1 (.in(gurads[1:0]), .out(or_reduce_1_out));
  // Or_Reduce #(.generic("bits := 4;")) or_reduce_2: pin names not known; wires that end beside it: {sticky, gurads}, or_reduce_2_p2
  or or_1 (or_1_out, or_reduce_1_out, sticky, fract);
  and and_1 (and_1_out, gurads[2], or_1_out);
  and and_2 (and_2_out, ~sign, or_reduce_2_p2);  // And
  and and_3 (and_3_out, sign, or_reduce_2_p2);
  Multiplexer #(.Selector_Bits(2)) multiplexer_1 (
    .sel(2'b00), .in_0(and_1_out), .in_1(and_2_out), .in_2(and_3_out), .in_3(1'b0), .out(round));

  // Notes on the sheet:
  //   round style
  //   00 - round nearest
  //   01 - round inf
  //   10 - round neginf
  //   11 - round zero
endmodule

/* Code that sets the parameters or builds the circuit:
round_style := 0;
*/
