// Digital circuit Float Classify.dig as structural Verilog
module Float_Classify (
  input  [31:0] arg,
  output [3:0] fptype
);

  wire and_1_out, and_2_out, and_3_out, and_4_out, and_5_out, and_6_out, and_7_out, and_8_out, and_9_out,
       and_10_out, and_reduce_1_p2, nor_reduce_1_p2, or_reduce_1_p2;

  // Or_Reduce #(.generic("bits := 23;")) or_reduce_1: pin names not known; wires that end beside it: arg[22:0], or_reduce_1_p2
  // And_Reduce #(.generic("bits := 8;")) and_reduce_1: pin names not known; wires that end beside it: arg[30:23], and_reduce_1_p2
  // NOr_Reduce #(.generic("bits := 8;")) nor_reduce_1: pin names not known; wires that end beside it: arg[30:23], nor_reduce_1_p2
  and and_1 (and_1_out, ~arg[22], and_reduce_1_p2, or_reduce_1_p2);  // And
  and and_2 (and_2_out, arg[22], and_reduce_1_p2, or_reduce_1_p2);
  and and_3 (and_3_out, ~arg[31], and_reduce_1_p2, ~or_reduce_1_p2);  // And
  and and_4 (and_4_out, arg[31], and_reduce_1_p2, ~or_reduce_1_p2);  // And
  and and_5 (and_5_out, ~arg[31], nor_reduce_1_p2, ~or_reduce_1_p2);  // And
  and and_6 (and_6_out, arg[31], nor_reduce_1_p2, ~or_reduce_1_p2);  // And
  and and_7 (and_7_out, ~arg[31], nor_reduce_1_p2, or_reduce_1_p2);  // And
  and and_8 (and_8_out, arg[31], nor_reduce_1_p2, or_reduce_1_p2);
  and and_9 (and_9_out, ~arg[31], ~and_reduce_1_p2, ~nor_reduce_1_p2);  // And
  and and_10 (and_10_out, arg[31], ~and_reduce_1_p2, ~nor_reduce_1_p2);  // And
  PriorityEncoder #(.Selector_Bits(4)) priorityencoder_1 (
    .in0(and_5_out), .in1(and_3_out), .in2(and_9_out), .in3(and_7_out), .in4(and_6_out), .in5(and_4_out),
    .in6(and_10_out), .in7(and_8_out), .in8(and_1_out), .in9(and_2_out), .in10(1'b0), .in11(1'b0),
    .in12(1'b0), .in13(1'b0), .in14(1'b0), .in15(1'b0), .num(fptype));  // open: any

  // Notes on the sheet:
  //   quiet_nan
  //   nan
  //   pos_inf
  //   neg_inf
  //   pos_zero
  //   neg_zero
  //   pos_denormal
  //   neg_denormal
  //   pos_normal
  //   neg_normal
  //   0 - pos_zero
  //   1 - pos_inf
  //   2 - pos_normal
  //   3 - pos_denormal
  //   4 - neg_zero
  //   5 - neg_inf
  //   6 - neg_normal
  //   7 - neg_denormal
  //   8 - quiet_nan
  //   9 - nan
  //   +0
  //   positive infinity
  //   positive normalized nonzero
  //   positive denormalized
  //   -0
  //   negative infinity
  //   negative normalized nonzero
  //   negative denormalized
  //   quiet NaN
  //   signaling NaN
endmodule
