// Digital circuit Float Comparator.dig as structural Verilog
module Float_Comparator (
  input  [31:0] a,
  input  [31:0] b,
  output gt,
  output eq,
  output lt
);

  wire and_1_out, and_2_out, and_3_out, and_5_out, and_6_out, and_7_out, and_8_out, and_9_out,
       and_reduce_1_p2, and_reduce_2_p2, comparator_1_eq, comparator_1_lt, nor_reduce_1_p2, nor_reduce_2_p2,
       or_1_out, or_2_out, or_3_out, xor_1_out, xor_2_out;

  Comparator #(.Bits(31)) comparator_1 (
    .a(a[30:0]), .b(b[30:0]), .eq(comparator_1_eq), .lt(comparator_1_lt));  // open: gt
  // And_Reduce #(.generic("bits := 8;")) and_reduce_1: pin names not known; wires that end beside it: a[30:23], and_reduce_1_p2
  // NOr_Reduce #(.generic("bits := 23;")) nor_reduce_1: pin names not known; wires that end beside it: a[22:0], nor_reduce_1_p2
  // And_Reduce #(.generic("bits := 8;")) and_reduce_2: pin names not known; wires that end beside it: b[30:23], and_reduce_2_p2
  // NOr_Reduce #(.generic("bits := 23;")) nor_reduce_2: pin names not known; wires that end beside it: b[22:0], nor_reduce_2_p2
  and and_1 (and_1_out, and_reduce_1_p2, ~nor_reduce_1_p2);  // And
  xor xor_1 (xor_1_out, comparator_1_lt, a[31]);
  xor xor_2 (xor_2_out, a[31], b[31]);
  and and_2 (and_2_out, ~a[31], b[31]);  // And
  and and_3 (and_3_out, and_reduce_2_p2, ~nor_reduce_2_p2);  // And
  and and_4 (eq, comparator_1_eq, ~xor_2_out);  // And
  and and_5 (and_5_out, xor_1_out, ~xor_2_out);  // And
  and and_6 (and_6_out, and_2_out, comparator_1_eq);
  or or_1 (or_1_out, and_5_out, and_2_out);
  or or_2 (or_2_out, and_6_out, comparator_1_lt);
  and and_7 (and_7_out, or_1_out, ~and_1_out, ~and_3_out);  // And
  and and_8 (and_8_out, and_1_out, and_3_out, or_2_out);
  and and_9 (and_9_out, and_1_out, ~and_3_out);  // And
  or or_3 (or_3_out, and_7_out, and_8_out, and_9_out);
  and and_10 (gt, ~eq, ~or_3_out);  // And
  and and_11 (lt, ~eq, or_3_out);  // And

  // Notes on the sheet:
  //   NaN
endmodule
