// Digital circuit Float Copysign.dig as structural Verilog
module Float_Copysign (
  input  [31:0] in,
  input  sgn,
  output [31:0] out
);

  // Pins of 31 and 32 bits meet at in

  assign out = {sgn, in[30:0]};
endmodule
