// Digital circuit Float Divide.dig as structural Verilog
module Float_Divide (
  input  [31:0] a,
  input  [31:0] b,
  output [31:0] q
);

  wire and_1_out, and_2_out, and_3_out, and_4_out, float_break_number_1_sign, float_break_number_2_sign,
       or_1_out, or_2_out, or_3_out, or_4_out, or_5_out, priorityencoder_1_any;
  wire [1:0] priorityencoder_1_num;
  wire [3:0] float_break_number_1_fptype, float_break_number_2_fptype;
  wire [4:0] rom_1_d, rom_2_d;
  wire [5:0] find_leftmost_1_pos, find_leftmost_2_pos, multiplexer_1_out, multiplexer_2_out, sub_1_s, sub_2_s;
  wire [7:0] float_break_number_1_exp, float_break_number_2_exp;
  wire [9:0] add_1_s, bitextender_1_out, bitextender_2_out, sub_3_s, sub_4_s, sub_5_s;
  wire [23:0] barrelshifter_1_out, barrelshifter_2_out, float_break_number_1_mnt, float_break_number_2_mnt;
  wire [27:0] div_1_q;
  wire [31:0] float_normalize_1_p5, multiplexer_3_out;
  wire [31:31] xor_1_out;
  wire [53:28] div_1_q_2;

  Float_Break_Number float_break_number_1 (
    .arg(a), .fptype(float_break_number_1_fptype), .sign(float_break_number_1_sign),
    .exp(float_break_number_1_exp), .mnt(float_break_number_1_mnt));
  Float_Break_Number float_break_number_2 (
    .arg(b), .fptype(float_break_number_2_fptype), .sign(float_break_number_2_sign),
    .exp(float_break_number_2_exp), .mnt(float_break_number_2_mnt));
  ROM #(.AddrBits(4), .Bits(5)) rom_1 (.A(float_break_number_1_fptype), .sel(1'b1), .D(rom_1_d));
  Find_Leftmost #(.generic("bits := 24;")) find_leftmost_1 (
    .arg(float_break_number_1_mnt), .val(1'b1), .pos(find_leftmost_1_pos));
  Find_Leftmost #(.generic("bits := 24;")) find_leftmost_2 (
    .arg(float_break_number_2_mnt), .val(1'b1), .pos(find_leftmost_2_pos));
  xor xor_1 (xor_1_out[31], float_break_number_1_sign, float_break_number_2_sign);
  BitExtender #(.outputBits(10)) bitextender_1 (.in(float_break_number_1_exp), .out(bitextender_1_out));
  BitExtender #(.outputBits(10)) bitextender_2 (.in(float_break_number_2_exp), .out(bitextender_2_out));
  ROM #(.AddrBits(4), .Bits(5)) rom_2 (.A(float_break_number_2_fptype), .sel(1'b1), .D(rom_2_d));
  Sub #(.Bits(6)) sub_1 (.a(6'b010111), .b(find_leftmost_1_pos), .c_i(1'b0), .s(sub_1_s));  // open: c_o
  Sub #(.Bits(6)) sub_2 (.a(6'b010111), .b(find_leftmost_2_pos), .c_i(1'b0), .s(sub_2_s));  // open: c_o
  or or_1 (or_1_out, rom_1_d[0], rom_1_d[1]);
  or or_2 (or_2_out, rom_2_d[0], rom_2_d[1]);
  or or_3 (or_3_out, rom_1_d[3], rom_1_d[4], rom_2_d[3], rom_2_d[4]);
  Multiplexer #(.Bits(6)) multiplexer_1 (.sel(rom_1_d[1]), .in_0({6{1'b0}}), .in_1(sub_1_s), .out(multiplexer_1_out));
  Multiplexer #(.Bits(6)) multiplexer_2 (.sel(rom_2_d[1]), .in_0({6{1'b0}}), .in_1(sub_2_s), .out(multiplexer_2_out));
  Sub #(.Bits(10)) sub_3 (
    .a({4'b0000, multiplexer_2_out}), .b({4'b0000, multiplexer_1_out}), .c_i(1'b0), .s(sub_3_s));  // open: c_o
  Sub #(.Bits(10)) sub_4 (.a(bitextender_1_out), .b(bitextender_2_out), .c_i(1'b0), .s(sub_4_s));  // open: c_o
  Add #(.Bits(10)) add_1 (.a(sub_3_s), .b(sub_4_s), .c_i(1'b0), .s(add_1_s));  // open: c_o
  and and_1 (and_1_out, rom_2_d[3], or_1_out);
  and and_2 (and_2_out, rom_1_d[2], or_2_out);
  and and_3 (and_3_out, or_1_out, rom_2_d[2]);
  and and_4 (and_4_out, or_2_out, rom_1_d[3]);
  BarrelShifter #(.Bits(24)) barrelshifter_1 (
    .in(float_break_number_1_mnt), .shift(multiplexer_1_out[4:0]), .out(barrelshifter_1_out));
  BarrelShifter #(.Bits(24)) barrelshifter_2 (
    .in(float_break_number_2_mnt), .shift(multiplexer_2_out[4:0]), .out(barrelshifter_2_out));
  Sub #(.Bits(10)) sub_5 (.a(add_1_s), .b(10'h2), .c_i(1'b0), .s(sub_5_s));  // open: c_o
  or or_4 (or_4_out, and_1_out, and_2_out);
  or or_5 (or_5_out, and_3_out, and_4_out);
  PriorityEncoder #(.Selector_Bits(2)) priorityencoder_1 (
    .in0(or_4_out), .in1(or_5_out), .in2(or_3_out), .in3(1'b0), .num(priorityencoder_1_num),
    .any(priorityencoder_1_any));
  Multiplexer #(.Selector_Bits(2), .Bits(32)) multiplexer_3 (
    .sel(priorityencoder_1_num), .in_0({xor_1_out[31], {31{1'b0}}}), .in_1({xor_1_out[31], 31'h7f800000}),
    .in_2(32'h7f800001), .in_3({32{1'b0}}), .out(multiplexer_3_out));
  Div #(.Bits(54)) div_1 (
    .a({barrelshifter_1_out, {30{1'b0}}}), .b({{27{1'b0}}, barrelshifter_2_out, 3'b000}),
    .q({div_1_q_2, div_1_q}));  // open: r
  // Float_Normalize #(.generic("exponent_bits := 10; round_style := args.round_style;")) float_normalize_1: pin names not known; wires that end beside it: div_1_q, sub_5_s, xor_1_out[31], 1'b1, float_normalize_1_p5
  Multiplexer #(.Bits(32)) multiplexer_4 (
    .sel(priorityencoder_1_any), .in_0(float_normalize_1_p5), .in_1(multiplexer_3_out), .out(q));

  // Notes on the sheet:
  //   Special Cases
  //   contents of rom_1 (hex, n*v repeats v):
  //   4,8,1,2,4,8,1,2,10,10
  //   Denormalization
  //   contents of rom_2 (hex, n*v repeats v):
  //   4,8,1,2,4,8,1,2,10,10
  //   if (a_nan | b_nan | a_inf | b_inf)
  //   q = quiet_nan
  //   else if (((a_normal | a_denormal) & b_zero) | (a_inf & (b_normal | b_denormal)))
  //   q = -1^sign * inf
  //   else if (((a_normal | a_denormal) & b_inf) | (a_zero & (b_normal | b_denormal)))
  //   q = -1^sign * zero
  //   else
  //   q = a / b
endmodule

/* Code that sets the parameters or builds the circuit:
round_style := 0;
*/
