// Digital circuit Float Multiply.dig as structural Verilog
module Float_Multiply (
  input  [31:0] a,
  input  [31:0] b,
  output [31:0] p
);

  wire and_1_out, and_2_out, float_break_number_1_sign, float_break_number_2_sign, or_1_out, or_2_out,
       or_3_out, or_reduce_1_p2, priorityencoder_1_any, priorityencoder_1_num, priorityencoder_2_any,
       priorityencoder_2_num;
  wire [3:0] float_break_number_1_fptype, float_break_number_2_fptype, rom_1_d, rom_2_d;
  wire [5:0] find_leftmost_1_pos, multiplexer_3_out, sub_1_s;
  wire [7:0] float_break_number_1_exp, float_break_number_2_exp;
  wire [9:0] add_1_s, add_2_s, bitextender_1_out, bitextender_2_out, sub_2_s;
  wire [19:0] mul_1_mul;
  wire [23:0] barrelshifter_1_out, float_break_number_1_mnt, float_break_number_2_mnt, multiplexer_1_out,
       multiplexer_2_out;
  wire [27:0] mul_1_mul_2;
  wire [31:0] float_normalize_1_p5, multiplexer_4_out;
  wire [31:31] xor_1_out;

  Float_Break_Number float_break_number_1 (
    .arg(a), .fptype(float_break_number_1_fptype), .sign(float_break_number_1_sign),
    .exp(float_break_number_1_exp), .mnt(float_break_number_1_mnt));
  Float_Break_Number float_break_number_2 (
    .arg(b), .fptype(float_break_number_2_fptype), .sign(float_break_number_2_sign),
    .exp(float_break_number_2_exp), .mnt(float_break_number_2_mnt));
  ROM #(.AddrBits(4), .Bits(4)) rom_1 (.A(float_break_number_1_fptype), .sel(1'b1), .D(rom_1_d));
  ROM #(.AddrBits(4), .Bits(4)) rom_2 (.A(float_break_number_2_fptype), .sel(1'b1), .D(rom_2_d));
  Multiplexer #(.Bits(24)) multiplexer_1 (
    .sel(priorityencoder_1_num), .in_0(float_break_number_2_mnt), .in_1(float_break_number_1_mnt),
    .out(multiplexer_1_out));
  Multiplexer #(.Bits(24)) multiplexer_2 (
    .sel(priorityencoder_1_num), .in_0(float_break_number_1_mnt), .in_1(float_break_number_2_mnt),
    .out(multiplexer_2_out));
  xor xor_1 (xor_1_out[31], float_break_number_1_sign, float_break_number_2_sign);
  Find_Leftmost #(.generic("bits := 24;")) find_leftmost_1 (
    .arg(multiplexer_2_out), .val(1'b1), .pos(find_leftmost_1_pos));
  BitExtender #(.outputBits(10)) bitextender_1 (.in(float_break_number_1_exp), .out(bitextender_1_out));
  BitExtender #(.outputBits(10)) bitextender_2 (.in(float_break_number_2_exp), .out(bitextender_2_out));
  or or_1 (or_1_out, rom_1_d[1], rom_2_d[1]);
  and and_1 (and_1_out, rom_1_d[2], rom_2_d[1]);
  and and_2 (and_2_out, rom_1_d[1], rom_2_d[2]);
  or or_2 (or_2_out, rom_1_d[3], rom_2_d[3]);
  PriorityEncoder priorityencoder_1 (
    .in0(rom_2_d[0]), .in1(rom_1_d[0]), .num(priorityencoder_1_num), .any(priorityencoder_1_any));
  Sub #(.Bits(6)) sub_1 (.a(6'b010111), .b(find_leftmost_1_pos), .c_i(1'b0), .s(sub_1_s));  // open: c_o
  or or_3 (or_3_out, and_1_out, and_2_out, or_2_out);
  Add #(.Bits(10)) add_1 (.a(bitextender_1_out), .b(bitextender_2_out), .c_i(1'b0), .s(add_1_s));  // open: c_o
  PriorityEncoder priorityencoder_2 (
    .in0(or_1_out), .in1(or_3_out), .num(priorityencoder_2_num), .any(priorityencoder_2_any));
  Multiplexer #(.Bits(6)) multiplexer_3 (
    .sel(priorityencoder_1_any), .in_0({6{1'b0}}), .in_1(sub_1_s), .out(multiplexer_3_out));
  Sub #(.Bits(10)) sub_2 (.a(add_1_s), .b({4'b0000, multiplexer_3_out}), .c_i(1'b0), .s(sub_2_s));  // open: c_o
  Multiplexer #(.Bits(32)) multiplexer_4 (
    .sel(priorityencoder_2_num), .in_0({xor_1_out[31], 31'h7f800000}), .in_1(32'h7f800001),
    .out(multiplexer_4_out));
  BarrelShifter #(.Bits(24)) barrelshifter_1 (
    .in(multiplexer_2_out), .shift(multiplexer_3_out[4:0]), .out(barrelshifter_1_out));
  Add #(.Bits(10)) add_2 (.a(sub_2_s), .b(10'h1), .c_i(1'b0), .s(add_2_s));  // open: c_o
  Mul #(.Bits(24)) mul_1 (.a(multiplexer_1_out), .b(barrelshifter_1_out), .mul({mul_1_mul_2, mul_1_mul}));
  // Or_Reduce #(.generic("bits := 20;")) or_reduce_1: pin names not known; wires that end beside it: mul_1_mul, or_reduce_1_p2
  // Float_Normalize #(.generic("exponent_bits := 10; round_style := args.round_style;")) float_normalize_1: pin names not known; wires that end beside it: mul_1_mul_2, add_2_s, xor_1_out[31], or_reduce_1_p2, float_normalize_1_p5
  Multiplexer #(.Bits(32)) multiplexer_5 (
    .sel(priorityencoder_2_any), .in_0(float_normalize_1_p5), .in_1(multiplexer_4_out), .out(p));

  // Notes on the sheet:
  //   Special Cases
  //   contents of rom_1 (hex, n*v repeats v):
  //   4,2,0,1,4,2,0,1,8,8
  //   Denormalization
  //   contents of rom_2 (hex, n*v repeats v):
  //   4,2,0,1,4,2,0,1,8,8
  //   if ((a_nan | b_nan) | (a_inf & b_zero) | (b_inf & a_zero))
  //   p = quiet_nan
  //   else if (a_inf | b_inf)
  //   p = -1^sign * inf
  //   else
  //   p = a * b
endmodule

/* Code that sets the parameters or builds the circuit:
round_style := 0;
*/
