// Digital circuit Float Negation.dig as structural Verilog
module Float_Negation (
  input  [31:0] in,
  output [31:0] out
);

  not not_1 (out[31], in[31]);

  assign out[30:0] = in[30:0];
endmodule
