// Digital circuit Float Normalize.dig as structural Verilog
module Float_Normalize (
  input  [27:0] fraction,
  input  [7:0] exponent,
  input  sign,
  input  sticky,
  output [31:0] res
);

  wire add_4_c_o, and_1_out, and_2_out, and_4_out, comparator_1_eq, comparator_1_gt, comparator_2_eq,
       comparator_2_lt, comparator_3_gt, comparator_4_lt, float_check_round_1_round, nor_reduce_1_p2,
       or_1_out, or_2_out, or_4_out;
  wire [1:0] and_3_out;
  wire [2:0] barrelshifter_1_out;
  wire [5:0] find_leftmost_1_pos, find_rightmost_1_pos;
  wire [7:7] not_1_out;
  wire [8:0] add_1_s, add_2_s, add_3_s, bitextender_1_out, bitextender_2_out, bitextender_3_out,
       multiplexer_1_out, neg_1_out, sub_1_s, sub_2_s;
  wire [10:0] multiplexer_2_out;
  wire [22:0] add_4_s, barrelshifter_1_out_2;
  wire [27:26] barrelshifter_1_out_3;

  Find_Leftmost #(.generic("bits := 28;")) find_leftmost_1 (.arg(fraction), .val(1'b1), .pos(find_leftmost_1_pos));
  Comparator #(.Signed("true"), .Bits(9), .generic("this.Bits = global.internal_exponent_bits;")) comparator_1 (
    .a(add_1_s), .b(9'h166), .gt(comparator_1_gt), .eq(comparator_1_eq));  // open: lt
  Comparator #(.Signed("true"), .Bits(9), .generic("this.Bits = global.internal_exponent_bits;")) comparator_2 (
    .a(add_1_s), .b(9'h180), .eq(comparator_2_eq), .lt(comparator_2_lt));  // open: gt
  Comparator #(.Signed("true"), .Bits(9), .generic("this.Bits = global.internal_exponent_bits;")) comparator_3 (
    .a(add_1_s), .b(9'h7e), .gt(comparator_3_gt));  // open: eq, lt
  BitExtender #(.inputBits(6), .outputBits(9), .generic("this.outputBits = global.internal_exponent_bits;")) bitextender_1 (
    .in(find_leftmost_1_pos), .out(bitextender_1_out));
  or or_1 (or_1_out, comparator_1_gt, comparator_1_eq);
  or or_2 (or_2_out, comparator_2_eq, comparator_2_lt);
  Sub #(.Bits(9), .generic("this.Bits = global.internal_exponent_bits;")) sub_1 (
    .a(bitextender_1_out), .b(9'h1a), .c_i(1'b0), .s(sub_1_s));  // open: c_o
  BitExtender #(.outputBits(9), .generic("this.inputBits = args.exponent_bits; this.outputBits = global.internal_exponent_bits;")) bitextender_2 (
    .in(exponent), .out(bitextender_2_out));
  // NOr_Reduce #(.generic("bits := 28;")) nor_reduce_1: pin names not known; wires that end beside it: fraction, nor_reduce_1_p2
  and and_1 (and_1_out, ~or_1_out, or_2_out);  // And
  and and_2 (and_2_out, or_1_out, ~nor_reduce_1_p2, or_2_out);  // And
  and and_3 (and_3_out[0], comparator_3_gt, ~nor_reduce_1_p2);  // And
  Add #(.Bits(9), .generic("this.Bits = global.internal_exponent_bits;")) add_1 (
    .a(sub_1_s), .b(bitextender_2_out), .c_i(1'b0), .s(add_1_s));  // open: c_o
  Add #(.Bits(9), .generic("this.Bits = global.internal_exponent_bits;")) add_2 (
    .a(bitextender_2_out), .b(9'h7f), .c_i(1'b0), .s(add_2_s));  // open: c_o
  or or_3 (and_3_out[1], and_1_out, nor_reduce_1_p2);
  Neg #(.Bits(9), .generic("this.Bits = global.internal_exponent_bits;")) neg_1 (.in(add_2_s), .out(neg_1_out));
  Multiplexer #(.Bits(9), .generic("this.Bits = global.internal_exponent_bits;")) multiplexer_1 (
    .sel(and_2_out), .in_0(add_1_s), .in_1(9'h180), .out(multiplexer_1_out));
  Multiplexer #(.Bits(9), .generic("this.Bits = global.internal_exponent_bits;")) multiplexer_2 (
    .sel(and_2_out), .in_0(sub_1_s), .in_1(neg_1_out), .out(multiplexer_2_out[8:0]));
  Find_Rightmost #(.generic("bits := 28;")) find_rightmost_1 (.arg(fraction), .val(1'b1), .pos(find_rightmost_1_pos));
  BarrelShifter #(.Bits(28), .barrelSigned("true"), .direction("right")) barrelshifter_1 (
    .in(fraction), .shift(multiplexer_2_out[5:0]),
    .out({barrelshifter_1_out_3, barrelshifter_1_out_2, barrelshifter_1_out}));
  BitExtender #(.inputBits(6), .outputBits(9), .generic("this.outputBits = global.internal_exponent_bits;")) bitextender_3 (
    .in(find_rightmost_1_pos), .out(bitextender_3_out));
  Comparator #(.Signed("true"), .Bits(9), .generic("this.Bits = global.internal_exponent_bits;")) comparator_4 (
    .a({9{1'b0}}), .b(multiplexer_2_out[8:0]), .lt(comparator_4_lt));  // open: gt, eq
  Sub #(.Bits(9), .generic("this.Bits = global.internal_exponent_bits;")) sub_2 (
    .a(bitextender_3_out), .b(multiplexer_2_out[8:0]), .c_i(1'b1), .s(sub_2_s));  // open: c_o
  and and_4 (and_4_out, comparator_4_lt, ~find_rightmost_1_pos[5], sub_2_s[8]);  // And
  or or_4 (or_4_out, and_4_out, sticky);
  Float_Check_Round #(.generic("round_style := args.round_style;")) float_check_round_1 (
    .fract(barrelshifter_1_out_2[0]), .gurads(barrelshifter_1_out), .sticky(or_4_out), .sign(sign),
    .round(float_check_round_1_round));
  Add #(.Bits(9), .generic("this.Bits = global.internal_exponent_bits;")) add_3 (
    .a({9{1'b0}}), .b(multiplexer_1_out), .c_i(add_4_c_o), .s(add_3_s));  // open: c_o
  Add #(.Bits(23)) add_4 (
    .a(barrelshifter_1_out_2), .b({23{1'b0}}), .c_i(float_check_round_1_round), .s(add_4_s), .c_o(add_4_c_o));
  not not_1 (not_1_out[7], add_3_s[7]);
  Multiplexer #(.Selector_Bits(2), .Bits(31)) multiplexer_3 (
    .sel(and_3_out), .in_0({not_1_out[7], add_3_s[6:0], add_4_s}), .in_1(31'h7f800000), .in_2({31{1'b0}}),
    .in_3({31{1'b0}}), .out(res[30:0]));
  // Pins of 9 and 11 bits meet at multiplexer_2_out

  assign res[31] = sign;

  // Notes on the sheet:
  //   overflow:1 & hidden:1 & mantissa:23 & guard:3
  //   if (norm exp < -154 | fraction == 0)
  //   result = -1^sign * zero
  //   if (-154 <= norm exp <= -128 & fraction != 0)
  //   float exp = -128
  //   float fraction = fraction >> (exp + 127)
  //   if (-128 < norm exp <= 126 & fraction != 0)
  //   float exp = norm exp
  //   float fraction = fraction << norm shift
  //   if (norm exp > 126 & fraction != 0)
  //   result = -1^sign * inf
  //   Boundary Check
  //   Exponent Normalization
  //   norm exp
  //   norm shift
  //   zero
  //   infinity
  //   Mantissa Normalization
  //   sticky shift
  //   Rounding
endmodule

/* Code that sets the parameters or builds the circuit:
exponent_bits := 8;
round_style := 0;
*/

/* Code that sets the parameters or builds the circuit:
if (args.exponent_bits < 8) {
    // minimal bits
    global.internal_exponent_bits := 9;
} else {
    // prevent overflow
    global.internal_exponent_bits := args.exponent_bits + 1;
}
*/
