// Digital circuit Float Scalb.dig as structural Verilog
module Float_Scalb (
  input  [31:0] in,
  input  [7:0] scale,
  output [31:0] out
);

  wire float_break_number_1_sign, rom_1_d;
  wire [3:0] float_break_number_1_fptype;
  wire [7:0] float_break_number_1_exp;
  wire [8:0] add_1_s, bitextender_1_out, bitextender_2_out;
  wire [23:0] float_break_number_1_mnt;
  wire [31:0] float_normalize_1_p5;

  Float_Break_Number float_break_number_1 (
    .arg(in), .fptype(float_break_number_1_fptype), .sign(float_break_number_1_sign),
    .exp(float_break_number_1_exp), .mnt(float_break_number_1_mnt));
  ROM #(.AddrBits(4)) rom_1 (.A(float_break_number_1_fptype), .sel(1'b1), .D(rom_1_d));
  BitExtender #(.outputBits(9), .generic("this.outputBits = global.exponent_bits;")) bitextender_1 (
    .in(float_break_number_1_exp), .out(bitextender_1_out));
  BitExtender #(.outputBits(9), .generic("this.inputBits = args.scale_bits; this.outputBits = global.exponent_bits;")) bitextender_2 (
    .in(scale), .out(bitextender_2_out));
  Add #(.Bits(9), .generic("this.Bits = global.exponent_bits;")) add_1 (
    .a(bitextender_1_out), .b(bitextender_2_out), .c_i(1'b0), .s(add_1_s));  // open: c_o
  // Float_Normalize #(.generic("exponent_bits := global.exponent_bits; round_style := args.round_style;")) float_normalize_1: pin names not known; wires that end beside it: {1'b0, float_break_number_1_mnt, 3'b000}, add_1_s, float_break_number_1_sign, 1'b0, float_normalize_1_p5
  Multiplexer #(.Bits(32)) multiplexer_1 (.sel(rom_1_d), .in_0(float_normalize_1_p5), .in_1(32'h7f800001), .out(out));

  // Notes on the sheet:
  //   contents of rom_1 (hex, n*v repeats v):
  //   0,0,0,0,0,0,0,0,1,1
endmodule

/* Code that sets the parameters or builds the circuit:
round_style := 0;
scale_bits := 4;
*/

/* Code that sets the parameters or builds the circuit:
if (args.scale_bits < 8) {
    // minimal bits
    global.exponent_bits := 9;
} else {
    // prevent overflow
    global.exponent_bits := args.scale_bits + 1;
}
*/
