// Digital circuit Float Square Root.dig as structural Verilog
module Float_Square_Root (
  input  [31:0] in,
  output [31:0] out
);

  wire [2:0] rom_1_d;
  wire [3:0] float_break_number_1_fptype;
  wire [7:0] barrelshifter_1_out, float_break_number_1_exp, sub_1_s;
  wire [23:0] float_break_number_1_mnt;
  wire [26:0] undriven;
  wire [31:0] float_normalize_1_res, multiplexer_1_out;
  wire [53:0] multiplexer_2_out;

  Float_Break_Number float_break_number_1 (
    .arg(in), .fptype(float_break_number_1_fptype), .exp(float_break_number_1_exp),
    .mnt(float_break_number_1_mnt));  // open: sign
  ROM #(.AddrBits(4), .Bits(3)) rom_1 (.A(float_break_number_1_fptype), .sel(1'b1), .D(rom_1_d));
  Multiplexer #(.Selector_Bits(2), .Bits(32)) multiplexer_1 (
    .sel(rom_1_d[1:0]), .in_0(32'h80000000), .in_1({32{1'b0}}), .in_2(32'h7f800000), .in_3(32'h7f800001),
    .out(multiplexer_1_out));
  Multiplexer #(.Bits(54)) multiplexer_2 (
    .sel(float_break_number_1_exp[0]), .in_0({float_break_number_1_mnt, {30{1'b0}}}),
    .in_1({1'b0, float_break_number_1_mnt, {29{1'b0}}}), .out(multiplexer_2_out));
  Sub #(.Bits(8)) sub_1 (.a(float_break_number_1_exp), .b(8'h1), .c_i(1'b0), .s(sub_1_s));  // open: c_o
  Square_Root #(.generic("bits := 54;")) square_root_1 (.in(multiplexer_2_out));
  BarrelShifter #(.barrelShifterMode("arithmetic"), .Bits(8), .direction("right")) barrelshifter_1 (
    .in(sub_1_s), .shift(4'b0001), .out(barrelshifter_1_out));
  Float_Normalize #(.generic("exponent_bits := 8; round_style := args.round_style;")) float_normalize_1 (
    .fraction({1'b0, undriven}), .exponent(barrelshifter_1_out), .sign(1'b0), .sticky(1'b0),
    .res(float_normalize_1_res));
  Multiplexer #(.Bits(32)) multiplexer_3 (
    .sel(rom_1_d[2]), .in_0(float_normalize_1_res), .in_1(multiplexer_1_out), .out(out));

  // Notes on the sheet:
  //   Special Cases
  //   contents of rom_1 (hex, n*v repeats v):
  //   5,6,0,0,4,7,7,7,7,7
  //   if (in == nan | in == quiet_nan
  //   | in == neg_normal | in == neg_denormal
  //   | in == neg_inf)
  //   out = quiet_nan
  //   else if (in == pos_inf)
  //   out = pos_inf
  //   else if (in == pos_zero)
  //   out = pos_zero
  //   else if (in == neg_zero)
  //   out = neg_zero
  //   else
  //   out = sqrt(in)
endmodule

/* Code that sets the parameters or builds the circuit:
round_style := 0;
*/
