// Digital circuit Float Subtract.dig as structural Verilog
module Float_Subtract (
  input  [31:0] a,
  input  [31:0] b,
  output [31:0] s
);

  wire [31:0] float_negation_1_out;

  Float_Negation float_negation_1 (.in(b), .out(float_negation_1_out));
  Float_Adder #(.generic("round_style := args.round_style;")) float_adder_1 (.a(a), .b(float_negation_1_out), .s(s));
endmodule

/* Code that sets the parameters or builds the circuit:
round_style := 0;
*/
