// Digital circuit Float To Integer.dig as structural Verilog
module Float_To_Integer (
  input  [31:0] in,
  output [15:0] out
);

  wire and_1_out, and_2_out, and_3_out, multiplexer_2_out, or_1_out, or_reduce_1_p2;
  wire [1:0] undriven_3;
  wire [2:0] multiplexer_1_out_2, sub_1_s_2;
  wire [3:0] float_classify_1_fptype, sub_1_s;
  wire [7:7] not_1_out;
  wire [8:0] bitextender_1_out;
  wire [8:7] sub_1_s_3;
  wire [15:0] add_1_s, fixed_resize_1_out, multiplexer_1_out, multiplexer_3_out, undriven, undriven_2;
  wire [18:0] barrelshifter_1_out;
  wire [18:16] undriven_4;

  Float_Classify float_classify_1 (.arg(in), .fptype(float_classify_1_fptype));
  not not_1 (not_1_out[7], in[30]);
  Fixed_Resize #(.generic("in_bits := 24; in_radix := 23; out_bits := args.bits; out_radix := args.bits - 1; round := false; saturate := false; signed := false;")) fixed_resize_1 (
    .in({1'b1, in[22:0]}), .out(fixed_resize_1_out));
  BitExtender #(.outputBits(9)) bitextender_1 (.in({not_1_out[7], in[29:23]}), .out(bitextender_1_out));
  Sub #(.Bits(9)) sub_1 (
    .a({9{1'b0}}), .b(bitextender_1_out), .c_i(1'b0), .s({sub_1_s_3, sub_1_s_2, sub_1_s}));  // open: c_o
  BarrelShifter #(.Bits(19), .direction("right"), .generic("this.Bits = args.bits + 3;")) barrelshifter_1 (
    .in({3'b000, fixed_resize_1_out}), .shift(sub_1_s), .out(barrelshifter_1_out));
  // Or_Reduce #(.generic("bits := 9 - bitsNeededFor(args.bits + 3) - 1;")) or_reduce_1: pin names not known; wires that end beside it: sub_1_s_2, or_reduce_1_p2
  Multiplexer #(.Bits(19), .generic("this.Bits = args.bits + 3;")) multiplexer_1 (
    .sel(or_reduce_1_p2), .in_0(barrelshifter_1_out), .in_1({undriven_4, {16{1'b0}}}),
    .out({multiplexer_1_out_2, multiplexer_1_out}));
  or or_1 (or_1_out, multiplexer_1_out[0], multiplexer_1_out_2[0], multiplexer_1_out_2[1]);
  Add #(.Bits(16), .generic("this.Bits = args.bits;")) add_1 (
    .a(multiplexer_1_out), .b({16{1'b0}}), .c_i(multiplexer_2_out), .s(add_1_s));  // open: c_o
  and and_1 (and_1_out, or_1_out, multiplexer_1_out_2[2]);
  and and_2 (and_2_out, multiplexer_1_out_2[2], ~in[31]);  // And
  and and_3 (and_3_out, multiplexer_1_out_2[2], in[31]);
  Multiplexer #(.Selector_Bits(2)) multiplexer_2 (
    .sel(2'b00), .in_0(and_1_out), .in_1(and_2_out), .in_2(and_3_out), .in_3(1'b0), .out(multiplexer_2_out));
  Multiplexer #(.Bits(16), .generic("this.Bits = args.bits;")) multiplexer_3 (
    .sel(sub_1_s_3[7]), .in_0(add_1_s), .in_1({16{1'b1}}), .out(multiplexer_3_out));
  Multiplexer #(.Selector_Bits(2), .Bits(16), .generic("this.Bits = args.bits;")) multiplexer_4 (
    .sel(undriven_3), .in_0({16{1'b0}}), .in_1({16{1'b0}}), .in_2(undriven_2), .in_3(undriven), .out(out));
  // Pins of 16 and 19 bits meet at {undriven_4, {16{1'b0}}}

  // Notes on the sheet:
  //   round style
  //   00 - round nearest
  //   01 - round inf
  //   10 - round neginf
  //   11 - round zero
  //   float to unsigned integer
  //   if (in == nan | in == quiet_nan)
  //   out = 0
  //   else if (in == pos_zero | in == neg_inf | in == neg_zero | in == neg_normal | in == pos_denormal | in == neg_denormal)
  //   out = 0
  //   else if (in == pos_inf)
  //   out = max
  //   else
  //   out = int(in)
  //   float to signed integer
  //   if (in == nan | in == quiet_nan)
  //   out = 0
  //   else if (in == pos_zero | in == neg_zero | in == pos_denormal | in == neg_denormal)
  //   out = 0
  //   else if (in == pos_inf | in == neg_inf)
  //   out = -1^sign * max
  //   else
  //   out = int(in)
endmodule

/* Code that sets the parameters or builds the circuit:
bits := 16;
signed := true;
round_style := 0;
*/

/* Code that sets the parameters or builds the circuit:
rom_lut := addComponent("ROM", 14, 4);
rom_lut.Bits = 2;
rom_lut.AddrBits = 4;
rom_lut.rotation = 1;

if (args.signed) {
    global.int_format := 2;
    
    rom_lut.Data = [1, 2, 3, 1, 1, 2, 3, 1, 0, 0, 0, 3, 3, 3, 3, 3];
    
    const_max := addComponent("Const", 1, -7);
    const_max.Bits = args.bits;
    const_max.Value = !(1 << (args.bits - 1));
    const_max.rotation = 3;
    const_max.intFormat = global.int_format;

    mux_max := addComponent("Multiplexer", 5, -6);
    mux_max.Bits = args.bits;

    not_max := addComponent("Not", 2, -4);
    not_max.Bits = args.bits;

    addWire(1, -7, 1, -4);
    addWire(1, -4, 2, -4);
    addWire(1, -6, 5, -6);
    addWire(4, -4, 5, -4);


    mux_val := addComponent("Multiplexer", 5, -2);
    mux_val.Bits = args.bits;

    neg_val := addComponent("Neg", 1, 0);
    neg_val.Bits = args.bits;

    addWire(0, 0, 1, 0);
    addWire(0, 0, 0, -2);
    addWire(0, -2, 5, -2);
    addWire(4, 0, 5, 0);


    s_val := addComponent("Splitter", 2, 2);
    s_val.'Input Splitting' = "" + args.bits;
    s_val.'Output Splitting' = (args.bits-1) + "-" + (args.bits-1);

    addWire(0, 0, 0, 2);
    addWire(0, 2, 2, 2);
    addWire(3, 2, 11, 2);
    addWire(11, 2, 11, 1);

    mux_val_max := addComponent("Multiplexer", 10, -1);
    mux_val_max.Bits = args.bits;

    addWire(7, -1, 10, -1);
    addWire(7, -5, 9, -5);
    addWire(9, -5, 9, 1);
    addWire(9, 1, 10, 1);
    addWire(9, -2, 13, -2);

    addWire(-13, 7, 8, 7);
    addWire(8, 7, 8, -3);
    addWire(8, -3, 6, -3);
    addWire(6, -3, 6, -4);
    addWire(8, 1, 6, 1);
    addWire(8, 1, 6, 1);
    addWire(6, 1, 6, 0);
} else {
    global.int_format := 1;
    
    rom_lut.Data = [1, 2, 3, 1, 1, 1, 1, 1, 0, 0, 0, 3, 3, 3, 3, 3];
    
    const_max := addComponent("Const", 13, -2);
    const_max.Bits = args.bits;
    const_max.Value = !(1 << args.bits);
    const_max.intFormat = global.int_format;
    
    addWire(0, 0, 12, 0);
}
*/
