// Digital circuit Absolute.dig as structural Verilog
// The Absolute returns the positive number of the input.
// {{de Der Absolute gibt die positive Zahl der Eingabe zurück.}}
module Absolute (
  input  in,
  output out
);

  wire neg_1_out;

  Neg #(.generic("this.Bits = args.bits;")) neg_1 (.in(in), .out(neg_1_out));
  Multiplexer #(.generic("this.Bits = args.bits;")) multiplexer_1 (.sel(in), .in_0(in), .in_1(neg_1_out), .out(out));
endmodule

/* Test case:
in out 
loop(i, 1 << 7)
    (i) (i)
end loop
loop(i, 1 << 7)
    (-i) (i)
end loop
*/

/* Code that sets the parameters or builds the circuit:
bits := 8;
*/
