// Digital circuit Adder Subtractor.dig as structural Verilog
// The Adder Subtractor returns "a + b" if "sub = 0", otherwise "a - b".
// {{de Der Adder Subtractor gibt "a + b" zurück, wenn "sub = 0" ist, sonst "a - b".}}
module Adder_Subtractor (
  input  a,
  input  b,
  input  sub,
  output [7:0] s
);

  wire multiplexer_1_out, not_1_out;

  not not_1 (not_1_out, b);
  Multiplexer #(.generic("this.Bits = args.bits;")) multiplexer_1 (
    .sel(sub), .in_0(b), .in_1(not_1_out), .out(multiplexer_1_out));
  Add #(.generic("this.Bits = args.bits;")) add_1 (.a(a), .b(multiplexer_1_out), .c_i(sub), .s(s));  // open: c_o
endmodule

/* Test case:
a b sub s
loop(aa, 1 << 4)
    loop(bb, 1 << 4)
        (aa) (bb) (0) (aa + bb)
    end loop
end loop
loop(aa, 1 << 4)
    loop(bb, 1 << 4)
        (aa) (bb) (1) (aa - bb)
    end loop
end loop
*/

/* Code that sets the parameters or builds the circuit:
bits := 8;
*/
