// Digital circuit Distance.dig as structural Verilog
// The Distance circuit outputs the absolute difference between a and b, and whether a or b is greater.
// {{de Der Distance Schaltkreis gibt den absoluten Differnez zwischen a und b aus, sowie ob a oder b größer ist.}}
module Distance (
  input  a,
  input  b,
  output d,
  output s
);

  wire neg_1_out, sub_1_c_o, sub_1_s, undriven, undriven_2;

  Sub #(.generic("this.Bits = args.bits;")) sub_1 (.a(a), .b(b), .c_i(1'b0), .s(sub_1_s), .c_o(sub_1_c_o));
  Neg #(.generic("this.Bits = args.bits;")) neg_1 (.in(sub_1_s), .out(neg_1_out));
  xnor xnor_1 (s, sub_1_c_o, ~undriven, undriven_2);  // XNOr
  Multiplexer #(.generic("this.Bits = args.bits;")) multiplexer_1 (.sel(s), .in_0(sub_1_s), .in_1(neg_1_out), .out(d));
endmodule

/* Test case:
a b d s
loop(aa, 1 << 4)
    loop(bb, 1 << 4)
        let ss = ite(aa >= bb, 0, 1);
	let dd = ite(aa >= bb, aa - bb, bb - aa);
        (aa) (bb) (dd) (ss)
    end loop
end loop
*/

/* Test case:
a b d s
loop(aa, 1 << 3)
    loop(bb, 1 << 3)
        let ss = ite(aa >= bb, 0, 1);
	let dd = ite(aa >= bb, aa - bb, bb - aa);
        (aa) (bb) (dd) (ss)
    end loop
end loop

loop(aa, 1 << 3)
    loop(bb, 1 << 3)
	let aa = -aa;
	let bb = -bb;
        let ss = ite(aa >= bb, 0, 1);
	let dd = ite(aa >= bb, aa - bb, bb - aa);
        (aa) (bb) (dd) (ss)
    end loop
end loop
*/

/* Code that sets the parameters or builds the circuit:
bits := 8;
signed := true;
*/

/* Code that sets the parameters or builds the circuit:
if (args.signed) {
    s1 := addComponent("Splitter", 5, 5);
    s1.'Input Splitting' = "" + args.bits;
    s1.'Output Splitting' = (args.bits-1) + "-" + (args.bits-1);

    s2 := addComponent("Splitter", 5, 6);
    s2.'Input Splitting' = "" + args.bits;
    s2.'Output Splitting' = (args.bits-1) + "-" + (args.bits-1);

    global.int_format := 2;
} else {
    g1 := addComponent("Ground", 6, 5);
    g1.rotation = 1;

    g2 := addComponent("Ground", 6, 6);
    g2.rotation = 1;

    global.int_format := 1;
}
*/
