// Digital circuit Find Leftmost.dig as structural Verilog
// Find Leftmost outputs the position of the highest "val" bit.
// If no bit was found, -1 is output.
// {{de 
// Find Leftmost gibt die Position des höchsten "val" Bits aus.
// Falls keine kein Bit gefunden wurde, wird -1 ausgegeben.
// }}
module Find_Leftmost (
  input  arg,
  input  val,
  output [3:0] pos
);

  wire multiplexer_1_out, not_1_out, priorityencoder_1_any;
  wire [3:0] priorityencoder_1_num;
  wire [3:1] undriven;

  not not_1 (not_1_out, arg);
  Multiplexer #(.generic("this.Bits = args.bits;")) multiplexer_1 (
    .sel(val), .in_0(not_1_out), .in_1(arg), .out(multiplexer_1_out));
  PriorityEncoder #(.generic("this.'Selector Bits' = global.bits;")) priorityencoder_1 (
    .num(priorityencoder_1_num[0]), .any(priorityencoder_1_any));  // open: in0, in1
  Multiplexer #(.Bits(4), .generic("this.Bits = global.bits + 1;")) multiplexer_2 (
    .sel(priorityencoder_1_any), .in_0(4'b0001), .in_1(priorityencoder_1_num), .out(pos));
  // Pins of 1 and 4 bits meet at priorityencoder_1_num
  // Pins of 4 and 8 bits meet at {undriven, 1'b0, priorityencoder_1_num}
  // Pins of 1 and 4 bits meet at {undriven, 1'b0}
endmodule

/* Test case:
arg    val pos
0b0100 1   2
0b0000 1   (-1)
0b0100 0   3
0b1111 0   (-1)
*/

/* Code that sets the parameters or builds the circuit:
bits := 8;
*/

/* Code that sets the parameters or builds the circuit:
global.bits := bitsNeededFor(args.bits-1);
n := 1 << global.bits;
m := n - args.bits;

s := addComponent("Splitter", 1, 0);
s.'Output Splitting' = "1*" + n;

if (m != 0) {
    s.'Input Splitting' = args.bits + "," + m;

    g := addComponent("Ground", 1, 1);
    g.rotation = 1;
    g.Bits = m;
} else {
    s.'Input Splitting' = "" + args.bits;
}

for (i := 0; i < n; i++) {
    addWire(2, i, 3, i);
}
*/
