// Digital circuit Find Rightmost.dig as structural Verilog
// Find Rightmost outputs the position of the lowest "val" bit.
// If no bit was found, -1 is output.
// {{de 
// Find Rightmost gibt die Position des niedrigsten "val" Bits aus.
// Falls keine kein Bit gefunden wurde, wird -1 ausgegeben.
// }}
module Find_Rightmost (
  input  [7:0] arg,
  input  val,
  output pos
);

  wire priorityencoder_1_any, priorityencoder_1_num;
  wire [3:0] not_2_out;
  wire [3:1] undriven;
  wire [7:0] multiplexer_1_out, not_1_out;

  assign not_1_out = ~arg;  // Not not_1, 8 bits wide
  Multiplexer #(.Bits(8), .generic("this.Bits = args.bits;")) multiplexer_1 (
    .sel(val), .in_0(not_1_out), .in_1(arg), .out(multiplexer_1_out));
  PriorityEncoder #(.generic("this.'Selector Bits' = global.bits;")) priorityencoder_1 (
    .num(priorityencoder_1_num), .any(priorityencoder_1_any));  // open: in0, in1
  assign not_2_out = ~{4{priorityencoder_1_num}};  // Not not_2, 4 bits wide
  Multiplexer #(.generic("this.Bits = global.bits + 1;")) multiplexer_2 (
    .sel(priorityencoder_1_any), .in_0(1'b1), .in_1({undriven, 1'b0, not_2_out}), .out(pos));
  // Pins of 1 and 4 bits meet at {undriven, 1'b0}
endmodule

/* Test case:
arg    val pos
0b0100 1   2
0b0000 1   (-1)
0b0100 0   0
0b1111 0   (-1)
*/

/* Code that sets the parameters or builds the circuit:
bits := 7;
*/

/* Code that sets the parameters or builds the circuit:
global.bits := bitsNeededFor(args.bits-1);
n := 1 << global.bits;
m := n - args.bits;

addWire(0, 0, 0, n-1);
addWire(0, n-1, 1, n-1);

s := addComponent("Splitter", 1, n-1);
s.mirror = true;
s.'Output Splitting' = "1*" + n;

if (m != 0) {
    s.'Input Splitting' = args.bits + "," + m;

    g := addComponent("Ground", 1, n-2);
    g.rotation = 1;
    g.Bits = m;
} else {
    s.'Input Splitting' = "" + args.bits;
}

for (i := 0; i < n; i++) {
    addWire(2, i, 3, i);
}
*/
