// Digital circuit Minimum.dig as structural Verilog
// Minimum outputs the smallest number of "a" or "b".
// {{de Minimum gibt die kleinste Zahl von "a" oder "b" aus.}}
module Minimum (
  input  [7:0] a,
  input  [7:0] b,
  output [7:0] min
);

  wire comparator_1_eq, comparator_1_gt, or_1_out;

  Comparator #(.Bits(8), .generic("this.Bits = args.bits; this.Signed = args.signed;")) comparator_1 (
    .a(a), .b(b), .gt(comparator_1_gt), .eq(comparator_1_eq));  // open: lt
  or or_1 (or_1_out, comparator_1_gt, comparator_1_eq);
  Multiplexer #(.Bits(8), .generic("this.Bits = args.bits;")) multiplexer_1 (
    .sel(or_1_out), .in_0(a), .in_1(b), .out(min));
endmodule

/* Test case:
a b min
loop(aa, 1 << 4)
    loop(bb, 1 << 4)
        let m = ite(aa < bb, aa, bb);
        (aa) (bb) (m)
    end loop
end loop
*/

/* Test case:
a b min
loop(aa, 1 << 3)
    loop(bb, 1 << 3)
        let m = ite(aa < bb, aa, bb);
        (aa) (bb) (m)
    end loop
end loop
*/

/* Code that sets the parameters or builds the circuit:
bits := 8;
signed := true;
*/

/* Code that sets the parameters or builds the circuit:
if (args.signed) {
    global.int_format := 2;
} else {
    global.int_format := 1;
}
*/
