// Digital circuit Square Root.dig as structural Verilog
// Square Root outputs the integer root.
// {{de Square Root gibt die Integer Wurzel aus..}}
module Square_Root (
  input  in
);

  wire not_1_out, sub_1_c_o;
  wire [1:0] multiplexer_1_out, sub_1_s, undriven;

  Sub #(.Bits(2)) sub_1 (.a(undriven), .b(2'b01), .c_i(1'b0), .s(sub_1_s), .c_o(sub_1_c_o));
  Multiplexer #(.Bits(2)) multiplexer_1 (.sel(not_1_out), .in_0(undriven), .in_1(sub_1_s), .out(multiplexer_1_out));
  not not_1 (not_1_out, sub_1_c_o);
endmodule

/* Test case:
in out
0  0
1  1
2  1
3  1
4  2
5  2
6  2
7  2
8  2
9  3
10 3
11 3
12 3
13 3
14 3
15 3
*/

/* Code that sets the parameters or builds the circuit:
bits := 8;
*/

/* Code that sets the parameters or builds the circuit:
even_bits := 2;
if (args.bits % 2 = 0) {
    even_bits = args.bits;
    addWire(-18, 0, -17, 0);
} else {
    even_bits = args.bits + 1;
    s := addComponent("Splitter", -18, 0);
    s.'Input Splitting'  = "" + args.bits + ",1";
    s.'Output Splitting' = "" + even_bits;
    
    gnd := addComponent("Ground", -19, 1);
    gnd.rotation = 1;
    
    addWire(-19, 1, -18, 1);
}

s := addComponent("Splitter", -14, 0);
s.'Input Splitting'  = "" + even_bits;
s.'Output Splitting' = "" + (even_bits - 2) + ",2";

N := even_bits / 2 - 1;
WIDTH := 20;

for (i := 0; i < N; i++) {
    iWIDTH := i * WIDTH;
    i1 := i + 1;
    i2 := i + 2;
    i3 := i + 3;

    s0 := addComponent("Splitter", iWIDTH + 0, 0);
    s0.'Input Splitting'  = "" + (even_bits - i1*2);
    s0.'Output Splitting' = "" + (even_bits - i2*2) + ",2";

    addWire(iWIDTH + 1, 0, iWIDTH + 20, 0);
    addWire(iWIDTH + 1, 1, iWIDTH + 4, 1);

    s1 := addComponent("Splitter", iWIDTH + 0, 2);
    s1.'Input Splitting'  = "" + i2;
    s1.'Output Splitting' = "" + i1 + ",1";
    s1.splitterSpreading = 5;
    
    addWire(iWIDTH + 1, 2, iWIDTH + 4, 2);
    addWire(iWIDTH + 1, 7, iWIDTH + 11, 7);
    addWire(iWIDTH + 11, 7, iWIDTH + 11, 6);
    addWire(iWIDTH + 11, 6, iWIDTH + 12, 6);

    s2 := addComponent("Splitter", iWIDTH + 4, 1);
    s2.'Input Splitting'  = "2," + i1;
    s2.'Output Splitting' = "" + i3;

    addWire(iWIDTH + 5, 1, iWIDTH + 15, 1);
    addWire(iWIDTH + 6, 1, iWIDTH + 6, 3);
    addWire(iWIDTH + 6, 3, iWIDTH + 7, 3);

    s3 := addComponent("Splitter", iWIDTH + 4, 4);
    s3.'Input Splitting'  = "2," + i1;
    s3.'Output Splitting' = "" + i3;

    const := addComponent("Const", iWIDTH + 2, 4);
    const.Bits = 2;
    const.Value = 1;

    addWire(iWIDTH + 2, 4, iWIDTH + 4, 4);
    addWire(iWIDTH + 5, 4, iWIDTH + 7, 4);
    addWire(iWIDTH + 3, 5, iWIDTH + 4, 5);
    addWire(iWIDTH + 3, 5, iWIDTH + 3, 8);

    s4 := addComponent("Splitter", iWIDTH + 17, 5);
    s4.'Input Splitting'  = "1," + i1;
    s4.'Output Splitting' = "" + i2;
    s4.splitterSpreading = 3;

    addWire(iWIDTH + 0, 8, iWIDTH + 17, 8);
    addWire(iWIDTH + 18, 5, iWIDTH + 19, 5);
    addWire(iWIDTH + 19, 5, iWIDTH + 19, 8);
    addWire(iWIDTH + 19, 8, iWIDTH + 20, 8);

    sub := addComponent("Sub", iWIDTH + 7, 3);
    sub.Bits = i3;

    gnd := addComponent("Ground", iWIDTH + 6, 5);
    gnd.rotation = 1;

    addWire(iWIDTH + 6, 5, iWIDTH + 7, 5);
    addWire(iWIDTH + 10, 3, iWIDTH + 15, 3);
    addWire(iWIDTH + 10, 4, iWIDTH + 11, 4);

    or := addComponent("Or", iWIDTH + 12, 4);
    or.inverterConfig = ["In_1"];
    or.wideShape = false;

    addWire(iWIDTH + 15, 5, iWIDTH + 17, 5);
    addWire(iWIDTH + 16, 5, iWIDTH + 16, 3);

    mux := addComponent("Multiplexer", iWIDTH + 15, 1);
    mux.Bits = i3;

    addWire(iWIDTH + 17, 2, iWIDTH + 20, 2);
}

out := addComponent("Out", N * WIDTH, 8);
out.intFormat = 1;
out.Bits = N + 1;
out.Label = "out";
*/
