// Digital circuit Edge Detector.dig as structural Verilog
// The Edge Detector emits a pulse when the edge changes.
// If "edge = 0", the falling edge is detected.
// {{de 
// Der Edge Detector gibt ein Pulse aus wenn die sich die Flanke ändert.
// Wenn "edge = 0" ist, wird die fallende Flakne dedectiert.
// }}
module Edge_Detector (
  input  D,
  input  C,
  output e
);

  wire d_ff_1_q, d_ff_2_q;

  D_FF d_ff_1 (.D(D), .C(C), .Q(d_ff_1_q));  // open: nQ
  D_FF d_ff_2 (.D(d_ff_1_q), .C(C), .Q(d_ff_2_q));  // open: nQ
  // And and_1 has open pins: In_1=open, In_2=open, out=e
endmodule

/* Test case rising:
C D  e
0 0  0
C 0  0

C 1  1
C 0  0

C 1  1
C 1  0
C 0  0
C 1  1
C 0  0
*/

/* Test case falling:
C D  e
0 0  0
C 0  0

C 1  0
C 0  1
C 0  0

C 1  0
C 1  0
C 0  1
C 1  0
C 0  1
*/

/* Code that sets the parameters or builds the circuit:
edge := 0;
*/

/* Code that sets the parameters or builds the circuit:
if (args.edge = 1) {
    addWire(12, -2, 13, -2);
} else {
    addWire(12, 0, 13, 0);
}
*/
