// Digital circuit For Loop.dig as structural Verilog
// The for-loop behaves like the while-loop the only difference is that it can iterate from "It_begin" to "It_end".
// {{de
// Die for-Schleife verhält sich wie die while-Schleife, mit dem einzigen Unterschied, dass sie von "It_begin" bis "It_end" iterieren kann.
// }}
module For_Loop (
  input  [7:0] It_begin,
  input  [7:0] It_end,
  input  start,
  input  stop,
  input  hold,
  input  C,
  input  clr,
  output [7:0] It,
  output done,
  output run,
  output init
);

  wire and_1_out, and_2_out, cond, or_1_out;
  wire [7:0] register_synchronous_1_q;

  and and_1 (and_1_out, run, cond);
  and and_2 (and_2_out, run, ~hold);  // And
  or or_1 (or_1_out, and_1_out, stop);
  CounterPreset #(.generic("this.Bits = args.bits;")) counterpreset_1 (
    .en(and_2_out), .C(C), .dir(1'b0), .in(It_begin), .ld(init), .clr(clr), .out(It));  // open: ovf
  Register_Synchronous #(.generic("bits := args.bits;")) register_synchronous_1 (
    .D(It_end), .en(init), .C(C), .clr(clr), .Q(register_synchronous_1_q));
  While_Loop while_loop_1 (
    .start(start), .stop(or_1_out), .hold(hold), .C(C), .clr(clr), .done(done), .run(run), .init(init));
  Comparator #(.Bits(8), .generic("this.Bits = args.bits;")) comparator_1 (
    .a(It), .b(register_synchronous_1_q), .eq(cond));  // open: gt, lt
endmodule

/* Code that sets the parameters or builds the circuit:
bits := 8;
*/

/* Test case:
C clr  It_begin It_end  start stop hold  It  done run init
0 0    0        0       0     0    0     0   0    0   0
C 1    0        0       0     0    0     0   0    0   0

C 0    0        5       1     0    0     0   0    0   1
C 0    0        5       0     0    0     0   0    1   0
C 0    0        0       0     0    0     1   0    1   0
C 0    0        0       0     0    0     2   0    1   0
C 0    0        0       0     0    0     3   0    1   0
C 0    0        0       0     0    1     3   0    1   0
C 0    0        0       0     0    0     4   0    1   0
C 0    0        0       0     0    0     5   1    0   0
C 0    0        0       0     0    0     5   0    0   0

C 1    0        0       0     0    0     0   0    0   0

C 0    0        0       1     0    0     0   0    0   1
C 0    42       69      0     0    0     42  0    1   0
C 0    0        0       0     0    0     43  0    1   0
C 0    0        0       0     0    0     44  0    1   0
C 0    0        0       0     0    0     45  0    1   0
C 0    0        0       0     0    0     46  0    1   0
C 0    0        0       0     1    0     47  1    0   0
C 0    0        0       0     0    0     47  0    0   0
*/
