// Digital circuit Trigger.dig as structural Verilog
// The Trigger stores the input and emits a pulse when the value changes.
// This circuit is modeled after the "sensitivity list" of VHDL and is compatible with the While and For Loop.
// {{de 
// Der Trigger speichert die Eingabe und gibt ein Pulse aus wenn die sich der Wert ändert.
// Dieser Schaltkreis ist der "sensitivity list" von VHDL nach nachempfunden und ist mit der While und For Schleife kompatibel.
// }}
module Trigger (
  input  D,
  input  C,
  output Q,
  output s
);

  wire comparator_1_eq;

  Register #(.generic("this.Bits = args.bits;")) register_1 (.D(D), .C(~C), .en(1'b1), .Q(Q));
  Comparator #(.generic("this.Bits = args.bits;")) comparator_1 (.a(D), .b(Q), .eq(comparator_1_eq));  // open: gt, lt
  not not_1 (s, comparator_1_eq);

  // Notes on the sheet:
  //   sensitivity
endmodule

/* Test case:
D C Q s
0 0 0 0
1 1 0 1
1 0 1 0
0 1 1 1
*/

/* Code that sets the parameters or builds the circuit:
bits := 8;
*/
