// Digital circuit Variable Clock Divider.dig as structural Verilog
// The Variable Clock Divider can be used to halve the frequency of C_i to any power of 2.
// {{de 
// Mit dem Variable Clock Divider lässt sich die Frequenz von C_i auf eine beliebige Potenz von 2 halbieren.
// }}
module Variable_Clock_Divider (
  input  C_i,
  input  div,
  output C_o
);

  wire comparator_1_eq, comparator_1_gt, counter_1_out, or_1_out, sub_1_s;

  Counter #(.generic("this.Bits = args.div_bits;")) counter_1 (
    .en(1'b1), .C(C_i), .clr(or_1_out), .out(counter_1_out));  // open: ovf
  Sub #(.generic("this.Bits = args.div_bits;")) sub_1 (.a(div), .b(1'b1), .c_i(1'b0), .s(sub_1_s));  // open: c_o
  Comparator #(.generic("this.Bits = args.div_bits;")) comparator_1 (
    .a(counter_1_out), .b(sub_1_s), .gt(comparator_1_gt), .eq(comparator_1_eq));  // open: lt
  or or_1 (or_1_out, comparator_1_gt, comparator_1_eq);
  Register register_1 (.D(~C_o), .C(C_i), .en(or_1_out), .Q(C_o));
endmodule

/* Code that sets the parameters or builds the circuit:
div_bits := 4;
*/

/* Test case:
C_i div  C_o

#divide by 5
0   5    0
C   5    0
C   5    0
C   5    0
C   5    0
C   5    1
C   5    1
C   5    1
C   5    1
C   5    1

#divide by 3
C   3    0
C   3    0
C   3    0
C   3    1
C   3    1
C   3    1
C   3    0
C   3    0
C   3    0
C   3    1
C   3    1
C   3    1

#divide by 2
C   2    0
C   2    0
C   2    1
C   2    1
C   2    0
C   2    0
*/
