// Digital circuit While Loop.dig as structural Verilog
// The while-loop has 4 states "idle", "init", "run" and "done" which are controled by "start", "stop" and "hold".
// The default state "idle" changes to "init" if "start" is 1.
// The "init" state changes to "run" if "stop" is 0 otherwise if "holds" is 0 to state "done".
// The "run" state changes to "done" if "stop" is 1 and "hold" is 0.
// The "done" state changes to "idle" after one clock cycle.
// {{de 
// Die while-Schleife hat 4 Zustände "idle", "init", "run" und "done", die durch "start", "stop" und "hold" gesteuert werden.
// Der Standardzustand "idle" wechselt zu "init", wenn "start" 1 ist.
// Der Zustand "init" wechselt zu "run", wenn "stop" gleich 0 ist, andernfalls, wenn "holds" gleich 0 ist, zum Zustand "done".
// Der Zustand "run" wechselt zu "done", wenn "stop" gleich 1 und "hold" gleich 0 ist.
// Der Zustand "done" geht nach einem Taktzyklus in den Zustand "idle" über.
// }}
module While_Loop (
  input  start,
  input  stop,
  input  hold,
  input  C,
  input  clr,
  output done,
  output run,
  output init
);

  wire and_1_out, and_2_out, and_3_out, and_4_out, and_5_out, and_6_out, and_10_out, and_11_out, not_1_out,
       not_2_out, not_3_out, not_4_out, not_5_out, not_6_out, or_1_out, or_2_out, Z_0_n, Z_1_n;

  not not_1 (not_1_out, stop);
  not not_2 (not_2_out, hold);
  not not_3 (not_3_out, Z_1_n);
  not not_4 (not_4_out, Z_0_n);
  and and_1 (and_1_out, Z_0_n, not_3_out, not_1_out);
  and and_2 (and_2_out, Z_0_n, not_3_out, not_2_out);
  and and_3 (and_3_out, not_4_out, Z_1_n);
  and and_4 (and_4_out, not_4_out, Z_1_n, stop, not_2_out);
  and and_5 (and_5_out, not_4_out, not_3_out, start);
  and and_6 (and_6_out, Z_0_n, not_3_out, stop);
  and and_7 (done, Z_0_n, Z_1_n);
  and and_8 (run, not_4_out, Z_1_n);
  and and_9 (init, Z_0_n, not_3_out);
  or or_1 (or_1_out, and_1_out, and_2_out, and_3_out);
  or or_2 (or_2_out, and_4_out, and_5_out, and_6_out);
  not not_5 (not_5_out, C);
  not not_6 (not_6_out, clr);
  and and_10 (and_10_out, not_6_out, or_1_out);
  and and_11 (and_11_out, not_6_out, or_2_out);
  D_FF d_ff_1 (.D(and_10_out), .C(not_5_out), .Q(Z_1_n));  // open: nQ
  D_FF d_ff_2 (.D(and_11_out), .C(not_5_out), .Q(Z_0_n));  // open: nQ
endmodule

/* Test case:
C clr  start stop hold  done run init
0 0    0     0    0     0    0   0
C 1    0     0    0     0    0   0

C 0    1     0    0     0    0   1
C 0    0     0    0     0    1   0
C 0    0     0    0     0    1   0
C 0    0     0    1     0    1   0
C 0    0     1    1     0    1   0
C 0    0     0    0     0    1   0
C 0    0     1    0     1    0   0
C 0    0     0    0     0    0   0

C 0    1     0    0     0    0   1
C 0    1     0    0     0    1   0
C 1    0     0    0     0    0   0
*/
