// Digital circuit Graph Plotter.dig as structural Verilog
// The Graph Plotter draws a continuous vertical line between two adjacent pixels.
// The circuit needs "2^y_bits" cycles of C_i per C_o to draw the graph.
// {{de
// Der Graph Plotter zeichnet eine durchgehende vertikale Linie zwischen zwei benachbarten Pixeln.
// Die Schaltung benötigt "2^y_bits" Zyklen von C_i pro C_o, um den Graphen zu zeichnen.
// }}
module Graph_Plotter (
  input  [7:0] y,
  input  color,
  input  en,
  input  C_i,
  output C_o
);

  wire and_1_out, and_2_out, and_3_out, and_4_out, comparator_1_lt, comparator_2_eq, comparator_2_gt,
       comparator_2_lt, comparator_3_eq, comparator_3_gt, comparator_3_lt, or_1_out, or_2_out, or_3_out;
  wire [7:0] multiplexer_1_out, multiplexer_2_out, not_1_out, register_1_q, register_2_q;
  wire [63:0] counter_1_out;
  wire [63:16] undriven;

  Variable_Clock_Divider #(.generic("div_bits := args.y_bits;")) variable_clock_divider_1 (
    .C_i(C_i), .div(1'b1), .C_o(C_o));
  assign not_1_out = ~y;  // Not not_1, 8 bits wide
  Counter #(.Bits(16), .generic("this.Bits = global.screen_bits;")) counter_1 (
    .en(en), .C(C_i), .clr(1'b0), .out(counter_1_out[15:0]));  // open: ovf
  Register #(.Bits(8), .generic("this.Bits = args.y_bits;")) register_1 (
    .D(not_1_out), .C(~C_o), .en(en), .Q(register_1_q));
  Register #(.Bits(8), .generic("this.Bits = args.y_bits;")) register_2 (
    .D(multiplexer_1_out), .C(~C_o), .en(en), .Q(register_2_q));
  Multiplexer #(.Bits(8), .generic("this.Bits = args.y_bits;")) multiplexer_1 (
    .sel(comparator_1_lt), .in_0(not_1_out), .in_1(register_1_q), .out(multiplexer_1_out));
  Multiplexer #(.Bits(8), .generic("this.Bits = args.y_bits;")) multiplexer_2 (
    .sel(comparator_1_lt), .in_0(multiplexer_1_out), .in_1(register_2_q), .out(multiplexer_2_out));
  Comparator #(.Bits(64), .generic("this.Bits = global.screen_bits;")) comparator_1 (
    .a({undriven, 16'hff}), .b(counter_1_out), .lt(comparator_1_lt));  // open: gt, eq
  Comparator #(.Bits(8), .generic("this.Bits = args.y_bits;")) comparator_2 (
    .a(multiplexer_1_out), .b(counter_1_out[7:0]), .gt(comparator_2_gt), .eq(comparator_2_eq),
    .lt(comparator_2_lt));
  Comparator #(.Bits(8), .generic("this.Bits = args.y_bits;")) comparator_3 (
    .a(multiplexer_2_out), .b(counter_1_out[7:0]), .gt(comparator_3_gt), .eq(comparator_3_eq),
    .lt(comparator_3_lt));
  or or_1 (or_1_out, comparator_2_gt, comparator_2_eq);
  or or_2 (or_2_out, comparator_3_gt, comparator_3_eq);
  and and_1 (and_1_out, or_3_out, en);
  GraphicCard #(.graphicHeight(256), .graphicWidth(256), .generic("this.Bits = args.color_bits; this.graphicWidth = 1 << args.x_bits; this.graphicHeight = 1 << args.y_bits;")) graphiccard_1 (
    .A({1'b0, counter_1_out[7:0], counter_1_out[15:8]}), .str(and_1_out), .C(C_i), .ld(1'b0), .B(1'b0),
    .D(color));
  and and_2 (and_2_out, or_1_out, comparator_3_lt);
  and and_3 (and_3_out, comparator_2_eq, comparator_3_eq);
  and and_4 (and_4_out, comparator_2_lt, or_2_out);
  or or_3 (or_3_out, and_2_out, and_3_out, and_4_out);
  // Pins of 16 and 64 bits meet at counter_1_out
  // Pins of 16 and 64 bits meet at {undriven, 16'hff}

  // Notes on the sheet:
  //   C_i: Hz: 256
endmodule

/* Code that sets the parameters or builds the circuit:
color_bits := 4;
x_bits := 8;
y_bits := 8;
*/

/* Code that sets the parameters or builds the circuit:
global.screen_bits := args.x_bits + args.y_bits;
*/
