// Digital circuit And Reduce.dig as structural Verilog
// The boolean and-reduction takes an array of bits and returns the logical "And" of all bits.
// {{de Die boolesche and-Reduktion nimmt ein Array von Bits und gibt das logische "And" aller Bits zurück.}}
module And_Reduce (
  input  [1:0] in,
  output out
);

  // And and_1 is placed but not wired
endmodule

/* Test case:
in out 
loop(i, 1 << 4)
    let x = (i & 1) & ((i >> 1) & 1) & ((i >> 2) & 1) & ((i >> 3) & 1);
    (i) (x)
end loop
*/

/* Code that sets the parameters or builds the circuit:
bits := 8;
*/

/* Code that sets the parameters or builds the circuit:
y := args.bits / 2;

addWire(8, y, 10, 0);

o := 0;
for (i := 0; i < args.bits; i++) {
    if ((i = y) & ((args.bits & 1) = 0)) {
        o = 1;
    }

    addWire(3, i, 5, i+o);
}
*/
