// Digital circuit Counter Asynchronous.dig as structural Verilog
module Counter_Asynchronous (
  input  en,
  input  C,
  input  clr,
  output [7:0] Q,
  output ovf
);

  wire add_1_c_o;
  wire [7:0] add_1_s, multiplexer_1_out;

  Add #(.Bits(8), .generic("this.Bits = args.bits;")) add_1 (.a(Q), .b(8'h1), .c_i(1'b0), .s(add_1_s), .c_o(add_1_c_o));
  Multiplexer #(.Bits(8), .generic("this.Bits = args.bits;")) multiplexer_1 (
    .sel(en), .in_0(Q), .in_1(add_1_s), .out(multiplexer_1_out));
  D_FF_AS #(.Bits(8), .generic("this.Bits = args.bits;")) d_ff_as_1 (
    .Set(1'b0), .D(multiplexer_1_out), .C(C), .Clr(clr), .Q(Q));  // open: nQ
  and and_1 (ovf, add_1_c_o, en);
endmodule

/* Code that sets the parameters or builds the circuit:
bits := 8;
*/
