// Digital circuit Counter Preset Asynchronous.dig as structural Verilog
module Counter_Preset_Asynchronous (
  input  en,
  input  C,
  input  dir,
  input  [7:0] in,
  input  ld,
  input  clr,
  output [7:0] out,
  output ovf
);

  wire add_1_c_o, xor_1_out;
  wire [7:0] add_1_s, multiplexer_1_out, multiplexer_2_out, multiplexer_3_out;

  Multiplexer #(.Bits(8), .generic("this.Bits = args.bits; this.Value = -1;")) multiplexer_1 (
    .sel(dir), .in_0(8'h1), .in_1({8{1'b1}}), .out(multiplexer_1_out));
  Add #(.Bits(8), .generic("this.Bits = args.bits;")) add_1 (
    .a(out), .b(multiplexer_1_out), .c_i(1'b0), .s(add_1_s), .c_o(add_1_c_o));
  Multiplexer #(.Bits(8), .generic("this.Bits = args.bits;")) multiplexer_2 (
    .sel(ld), .in_0(out), .in_1(in), .out(multiplexer_2_out));
  Multiplexer #(.Bits(8), .generic("this.Bits = args.bits;")) multiplexer_3 (
    .sel(en), .in_0(multiplexer_2_out), .in_1(add_1_s), .out(multiplexer_3_out));
  xor xor_1 (xor_1_out, dir, add_1_c_o);
  D_FF_AS #(.Bits(8), .generic("this.Bits = args.bits;")) d_ff_as_1 (
    .Set(1'b0), .D(multiplexer_3_out), .C(C), .Clr(clr), .Q(out));  // open: nQ
  and and_1 (ovf, xor_1_out, en);
endmodule

/* Code that sets the parameters or builds the circuit:
bits := 8;
*/
