// Digital circuit Register Asynchronous.dig as structural Verilog
module Register_Asynchronous (
  input  [7:0] D,
  input  en,
  input  C,
  input  clr,
  output [7:0] Q
);

  wire [7:0] multiplexer_1_out;

  Multiplexer #(.Bits(8), .generic("this.Bits = args.bits;")) multiplexer_1 (
    .sel(en), .in_0(Q), .in_1(D), .out(multiplexer_1_out));
  D_FF_AS #(.generic("this.Bits = args.bits;")) d_ff_as_1 (
    .Set(1'b0), .D(multiplexer_1_out), .C(C), .Clr(clr), .Q(Q));  // open: nQ
endmodule

/* Code that sets the parameters or builds the circuit:
bits := 8;
*/
