// Digital circuit Register Synchronous.dig as structural Verilog
module Register_Synchronous (
  input  [7:0] D,
  input  en,
  input  C,
  input  clr,
  output [7:0] Q
);

  wire or_1_out;
  wire [7:0] multiplexer_1_out;

  Multiplexer #(.Bits(8), .generic("this.Bits = args.bits;")) multiplexer_1 (
    .sel(clr), .in_0(D), .in_1({8{1'b0}}), .out(multiplexer_1_out));
  or or_1 (or_1_out, clr, en);
  Register #(.Bits(8), .generic("this.Bits = args.bits;")) register_1 (
    .D(multiplexer_1_out), .C(C), .en(or_1_out), .Q(Q));
endmodule

/* Code that sets the parameters or builds the circuit:
bits := 8;
*/

/* Test case:
C en clr D  Q
0 0  0   0  0
C 0  0   0  0

C 1  0   42 42
C 0  0   0  42

0 0  1   0  42
0 1  1   0  42
C 0  1   0  0
*/
