// Digital circuit Shift Register Asynchronous.dig as structural Verilog
// direction: 
//     true - left shift
//     false - right shift
module Shift_Register_Asynchronous (
  input  s_in,
  input  [7:0] p_in,
  input  ld,
  input  en,
  input  C,
  input  clr,
  output s_out,
  output [7:0] p_out
);

  wire or_1_out;
  wire [7:0] multiplexer_1_out, undriven;

  Multiplexer #(.Bits(8), .generic("this.Bits = args.bits;")) multiplexer_1 (
    .sel(ld), .in_0(undriven), .in_1(p_in), .out(multiplexer_1_out));
  or or_1 (or_1_out, en, ld);
  Register_Asynchronous #(.generic("bits := args.bits;")) register_asynchronous_1 (
    .D(multiplexer_1_out), .en(or_1_out), .C(C), .clr(clr), .Q(p_out));
endmodule

/* Code that sets the parameters or builds the circuit:
bits := 8;
direction := "l";
*/

/* Code that sets the parameters or builds the circuit:
s1 := addComponent("Splitter", 4, 4);
s1.'Output Splitting' = "" + args.bits;

s2 := addComponent("Splitter", 20, 6);
s2.'Input Splitting' = "" + args.bits;
s2.rotation = 1;

if (args.direction = "l") {
    s1.'Input Splitting' = "1," + (args.bits-1);
    s1.mirror = true;

    s2.'Output Splitting' = (args.bits-1) + ",1";
    s2.mirror = false;

    addWire(3,3,4,3);
    addWire(2,4,4,4);

    addWire(19,2,20,2);
    addWire(20,2,20,5);
    addWire(21,2,21,5);
} else if (args.direction = "r") {
    s1.'Input Splitting' = (args.bits-1) + ",1";
    s1.mirror = false;

    s2.'Output Splitting' = "1," + (args.bits-1);
    s2.mirror = true;

    addWire(2,4,2,5);
    addWire(2,5,4,5);
    addWire(3,3,3,4);
    addWire(3,4,4,4);

    addWire(19,2,19,5);
    addWire(20,2,21,2);
    addWire(20,2,20,5);
} else {
    panic("Direction must be 'l' or 'r'!");
}
*/
